// Logisim project 4_cycle_adder.circ as structural Verilog: 1 circuit, main circuit main
module main (
  input  [15:0] x,
  input  [15:0] y,
  output [15:0] out_3
);

  wire adder_1_cout, and_1_out, carryGiver_q, clock_1_out, demultiplexer_2_out0, demultiplexer_2_out1,
       demultiplexer_2_out2, demultiplexer_2_out3, or_1_out;
  wire [1:0] CTRL_q, not_1_out;
  wire [3:0] adder_1_out, demultiplexer_1_out0, demultiplexer_1_out1, demultiplexer_1_out2,
       demultiplexer_1_out3;
  wire [7:0] multiplexer_1_out;

  Clock clock_1 (.out(clock_1_out));
  xor xor_1 (not_1_out[1], CTRL_q[0], CTRL_q[1]);
  not not_1 (not_1_out[0], CTRL_q[0]);
  or or_1 (or_1_out, CTRL_q[0], CTRL_q[1]);
  Multiplexer #(.select(2), .width(8)) multiplexer_1 (
    .in0({y[3:0], x[3:0]}), .in1({y[7:4], x[7:4]}), .in2({y[11:8], x[11:8]}), .in3({y[15:12], x[15:12]}),
    .out(multiplexer_1_out), .sel(CTRL_q));
  D_Flip_Flop carryGiver (.D(adder_1_cout), .clk(clock_1_out), .Q(carryGiver_q), .reset(1'b0));  // open: Qn, preset
  Register #(.width(2)) CTRL (.D(not_1_out), .en(1'b1), .clk(clock_1_out), .Q(CTRL_q), .clr(1'b0));
  and and_1 (and_1_out, carryGiver_q, or_1_out);
  Demultiplexer #(.select(2), .width(4)) demultiplexer_1 (
    .out0(demultiplexer_1_out0), .out1(demultiplexer_1_out1), .out2(demultiplexer_1_out2),
    .out3(demultiplexer_1_out3), .in(adder_1_out), .sel(CTRL_q));
  Adder #(.width(4)) adder_1 (
    .a(multiplexer_1_out[3:0]), .b(multiplexer_1_out[7:4]), .out(adder_1_out), .cin(and_1_out),
    .cout(adder_1_cout));
  Demultiplexer #(.select(2)) demultiplexer_2 (
    .out0(demultiplexer_2_out0), .out1(demultiplexer_2_out1), .out2(demultiplexer_2_out2),
    .out3(demultiplexer_2_out3), .in(1'b1), .sel(CTRL_q));
  Register #(.width(4)) register_1 (
    .D(demultiplexer_1_out0), .en(demultiplexer_2_out0), .clk(clock_1_out), .Q(out_3[3:0]));  // open: clr
  Register #(.width(4)) register_2 (
    .D(demultiplexer_1_out2), .en(demultiplexer_2_out2), .clk(clock_1_out), .Q(out_3[11:8]));  // open: clr
  Register #(.width(4)) register_3 (
    .D(demultiplexer_1_out1), .en(demultiplexer_2_out1), .clk(clock_1_out), .Q(out_3[7:4]));  // open: clr
  Register #(.width(4)) register_4 (
    .D(demultiplexer_1_out3), .en(demultiplexer_2_out3), .clk(clock_1_out), .Q(out_3[15:12]));  // open: clr
endmodule
