// Logisim project Ejercicio2.circ as structural Verilog: 4 circuits, main circuit main
module main (
  input  [3:0] DIN,
  input  dmux,
  input  ld1,
  input  ld2,
  input  resta_suma,
  input  ld3,
  input  CLK,
  input  RESET,
  output z,
  output [3:0] DOUT
);

  wire [3:0] demultiplexer_1_out0, demultiplexer_1_out1, register_1_q, register_2_q, unidadaritmetica_1_r3;

  Register #(.width(4)) register_1 (.D(demultiplexer_1_out0), .en(ld1), .clk(CLK), .Q(register_1_q), .clr(RESET));
  Demultiplexer #(.width(4)) demultiplexer_1 (
    .out0(demultiplexer_1_out0), .out1(demultiplexer_1_out1), .in(DIN), .sel(dmux));
  Register #(.width(4)) register_2 (.D(demultiplexer_1_out1), .en(ld2), .clk(CLK), .Q(register_2_q), .clr(RESET));
  Register #(.width(4)) register_3 (.D(unidadaritmetica_1_r3), .en(ld3), .clk(CLK), .Q(DOUT), .clr(RESET));
  UnidadAritmetica unidadaritmetica_1 (
    .R1(register_1_q), .R2(register_2_q), .sel(resta_suma), .R3(unidadaritmetica_1_r3), .z(z));
endmodule

module UnidadAritmetica (
  input  sel,
  input  [3:0] R1,
  input  [3:0] R2,
  output [3:0] R3,
  output z
);

  wire [3:0] adder_1_out, subtractor_1_out;

  Subtractor #(.width(4)) subtractor_1 (.a(R1), .b(R2), .out(subtractor_1_out));  // open: bin, bout
  Adder #(.width(4)) adder_1 (.a(R1), .b(R2), .out(adder_1_out));  // open: cin, cout
  Multiplexer #(.width(4)) multiplexer_1 (.in0(subtractor_1_out), .in1(adder_1_out), .out(R3), .sel(sel));
  Comparator #(.width(4)) comparator_1 (.a(R3), .b(4'b0000), .eq(z));  // open: gt, lt
endmodule

module UC (
  input  dato_valido,
  input  z,
  input  CLK,
  input  RESET,
  output Id3,
  output resta_suma,
  output Id2,
  output Id1,
  output DMUX,
  output FIN
);

  wire and_1_out, and_2_out, and_3_out, and_4_out, and_5_out, and_6_out, and_7_out, and_8_out, not_1_out,
       not_2_out, not_3_out, not_4_out;
  wire [2:0] or_1_out, register_1_q;

  not not_1 (not_1_out, register_1_q[2]);
  not not_2 (not_2_out, register_1_q[1]);
  not not_3 (not_3_out, register_1_q[0]);
  not not_4 (not_4_out, z);
  and and_1 (and_1_out, not_1_out, not_2_out, not_3_out, dato_valido);
  and and_2 (and_2_out, not_1_out, register_1_q[1], not_3_out);
  and and_3 (and_3_out, not_1_out, register_1_q[1], register_1_q[0], z);
  and and_4 (and_4_out, register_1_q[2], not_2_out);
  and and_5 (and_5_out, not_1_out, register_1_q[1], not_3_out);
  and and_6 (and_6_out, not_1_out, not_2_out, register_1_q[0]);
  and and_7 (and_7_out, not_1_out, register_1_q[1], register_1_q[0]);
  and and_8 (and_8_out, register_1_q[2], not_2_out);
  or or_1 (or_1_out[0], and_1_out, and_2_out, and_3_out, and_4_out);
  or or_2 (or_1_out[1], and_5_out, and_6_out);
  or or_3 (or_1_out[2], and_7_out, and_8_out);
  Register #(.width(3)) register_1 (.D(or_1_out), .en(1'b1), .clk(CLK), .Q(register_1_q), .clr(RESET));
  ROM #(.addrWidth(3), .dataWidth(6)) rom_1 (.addr(register_1_q), .data({FIN, DMUX, Id1, Id2, resta_suma, Id3}));

  // Notes on the sheet:
  //   contents of rom_1 (hex, n*v repeats v):
  //   0 8 14 0 1 20
endmodule

module Ejercicio2 (
  input  [3:0] DATAIN,
  input  dato_valido,
  input  RESET,
  output FIN,
  output [3:0] out_5
);

  wire clock_1_out, main_1_z, uc_1_dmux, uc_1_id1, uc_1_id2, uc_1_id3, uc_1_resta_suma;

  Clock clock_1 (.out(clock_1_out));
  UC uc_1 (
    .dato_valido(dato_valido), .z(main_1_z), .CLK(clock_1_out), .RESET(RESET), .Id3(uc_1_id3),
    .resta_suma(uc_1_resta_suma), .Id2(uc_1_id2), .Id1(uc_1_id1), .DMUX(uc_1_dmux), .FIN(FIN));
  main main_1 (
    .DIN(DATAIN), .dmux(uc_1_dmux), .ld1(uc_1_id1), .ld2(uc_1_id2), .resta_suma(uc_1_resta_suma),
    .ld3(uc_1_id3), .CLK(clock_1_out), .RESET(RESET), .z(main_1_z), .DOUT(out_5));
endmodule
