// Logisim project Ejercicio3.circ as structural Verilog: 5 circuits, main circuit UPGSmall
module UPGSmall (
  input  [7:0] DATAIN,
  input  InALU,
  input  Reset,
  input  [1:0] AddrD,
  input  WrD,
  input  [1:0] AddrA,
  input  [1:0] AddrB,
  input  [3:0] IMMED,
  input  RbImm,
  input  [1:0] F,
  input  CmpAL,
  input  CLK,
  output [7:0] DATAOUT,
  output z
);

  wire [7:0] alu_1_w, bit_extender_1_out, multiplexer_1_out, multiplexer_2_out, regfile_1_a;

  assign bit_extender_1_out = {{4{IMMED[3]}}, IMMED};  // Bit_Extender bit_extender_1
  // Probe on regfile_1_a
  // Probe on alu_1_w
  Multiplexer #(.width(8)) multiplexer_1 (.in0(DATAIN), .in1(alu_1_w), .out(multiplexer_1_out), .sel(InALU));
  RegFile regfile_1 (
    .clk(CLK), .WrD(WrD), .AddrD(AddrD), .D(multiplexer_1_out), .Reset(Reset), .AddrB(AddrB), .AddrA(AddrA),
    .A(regfile_1_a), .B(DATAOUT));
  Multiplexer #(.width(8)) multiplexer_2 (
    .in0(bit_extender_1_out), .in1(DATAOUT), .out(multiplexer_2_out), .sel(RbImm));
  // Probe on multiplexer_2_out
  ALU alu_1 (.CmpAL(CmpAL), .A(regfile_1_a), .B(multiplexer_2_out), .F(F), .z(z), .W(alu_1_w));
endmodule

module RegFile (
  input  [7:0] D,
  input  WrD,
  input  [1:0] AddrD,
  input  clk,
  input  Reset,
  input  [1:0] AddrB,
  input  [1:0] AddrA,
  output [7:0] A,
  output [7:0] B
);

  wire decoder_1_out0, decoder_1_out1, decoder_1_out2, decoder_1_out3;
  wire [7:0] register_1_q, register_2_q, register_3_q, register_4_q;

  Decoder #(.select(2)) decoder_1 (
    .out0(decoder_1_out0), .out1(decoder_1_out1), .out2(decoder_1_out2), .out3(decoder_1_out3), .sel(AddrD),
    .en(WrD));
  Register register_1 (.D(D), .en(decoder_1_out0), .clk(clk), .Q(register_1_q), .clr(Reset));
  Register register_2 (.D(D), .en(decoder_1_out1), .clk(clk), .Q(register_2_q), .clr(Reset));
  Register register_3 (.D(D), .en(decoder_1_out2), .clk(clk), .Q(register_3_q), .clr(Reset));
  Register register_4 (.D(D), .en(decoder_1_out3), .clk(clk), .Q(register_4_q), .clr(Reset));
  Multiplexer #(.select(2), .width(8)) multiplexer_1 (
    .in0(register_1_q), .in1(register_2_q), .in2(register_3_q), .in3(register_4_q), .out(B), .sel(AddrB));
  Multiplexer #(.select(2), .width(8)) multiplexer_2 (
    .in0(register_1_q), .in1(register_2_q), .in2(register_3_q), .in3(register_4_q), .out(A), .sel(AddrA));
endmodule

module ALU (
  input  [7:0] A,
  input  [7:0] B,
  input  [1:0] F,
  input  CmpAL,
  output [7:0] W,
  output z
);

  wire comparator_1_eq, comparator_1_lt, or_1_out;
  wire [7:0] adder_1_out, and_1_out, bit_extender_1_out, bit_extender_2_out, bit_extender_3_out,
       multiplexer_1_out, multiplexer_2_out, not_1_out, subtractor_1_out;

  // Probe on A
  // Probe on B
  assign not_1_out = ~A;  // NOT_Gate not_1, 8 bits wide
  assign and_1_out = B & A;  // AND_Gate and_1, 8 bits wide
  Subtractor subtractor_1 (.a(A), .b(B), .out(subtractor_1_out));  // open: bin, bout
  Adder adder_1 (.a(B), .b(A), .out(adder_1_out));  // open: cin, cout
  Comparator comparator_1 (.a(B), .b(A), .eq(comparator_1_eq), .lt(comparator_1_lt));  // open: gt
  or or_1 (or_1_out, comparator_1_eq, comparator_1_lt);
  assign bit_extender_1_out = {{7{1'b0}}, or_1_out};  // Bit_Extender bit_extender_1
  assign bit_extender_2_out = {{7{1'b0}}, comparator_1_lt};  // Bit_Extender bit_extender_2
  assign bit_extender_3_out = {{7{1'b0}}, comparator_1_eq};  // Bit_Extender bit_extender_3
  Multiplexer #(.select(2), .width(8)) multiplexer_1 (
    .in0(not_1_out), .in1(and_1_out), .in2(subtractor_1_out), .in3(adder_1_out), .out(multiplexer_1_out),
    .sel(F));
  Multiplexer #(.select(2), .width(8)) multiplexer_2 (
    .in0(bit_extender_1_out), .in1(bit_extender_2_out), .in2(bit_extender_3_out), .in3(B),
    .out(multiplexer_2_out), .sel(F));
  Multiplexer #(.width(8)) multiplexer_3 (.in0(multiplexer_1_out), .in1(multiplexer_2_out), .out(W), .sel(CmpAL));
  Comparator comparator_2 (.a(W), .b({8{1'b0}}), .eq(z));  // open: gt, lt
endmodule

module UC (
  input  z,
  input  CLK,
  input  RESET,
  output InALU,
  output WrD,
  output [3:0] IMMED,
  output RbImm,
  output [1:0] AddrB,
  output [1:0] AddrA,
  output [1:0] AddrD,
  output [1:0] F,
  output CmpAL
);

  wire [2:0] PC_q, rom_1_data;

  ROM #(.addrWidth(4), .dataWidth(3)) rom_1 (.addr({PC_q, z}), .data(rom_1_data));
  Register #(.width(3)) PC (.D(rom_1_data), .en(1'b1), .clk(CLK), .Q(PC_q), .clr(RESET));
  ROM #(.addrWidth(3), .dataWidth(16)) rom_2 (
    .addr(PC_q), .data({CmpAL, F, AddrD, AddrA, AddrB, RbImm, IMMED, WrD, InALU}));

  // Notes on the sheet:
  //   contents of rom_1 (hex, n*v repeats v):
  //   1 1 2 2 6 3 5 4 4*2 6 6
  //   contents of rom_2 (hex, n*v repeats v):
  //   2 802 d0c3 b243 40c3 4a43
endmodule

module PPG (
  input  [7:0] DATAIN,
  input  RESET,
  output [7:0] DATAOUT
);

  wire clock_1_out, uc_1_cmpal, uc_1_inalu, uc_1_rbimm, uc_1_wrd, upgsmall_1_z;
  wire [1:0] uc_1_addra, uc_1_addrb, uc_1_addrd, uc_1_f;
  wire [3:0] uc_1_immed;

  Clock clock_1 (.out(clock_1_out));
  UC uc_1 (
    .z(upgsmall_1_z), .CLK(clock_1_out), .RESET(RESET), .InALU(uc_1_inalu), .WrD(uc_1_wrd),
    .IMMED(uc_1_immed), .RbImm(uc_1_rbimm), .AddrB(uc_1_addrb), .AddrA(uc_1_addra), .AddrD(uc_1_addrd),
    .F(uc_1_f), .CmpAL(uc_1_cmpal));
  UPGSmall upgsmall_1 (
    .DATAIN(DATAIN), .InALU(uc_1_inalu), .Reset(RESET), .AddrD(uc_1_addrd), .WrD(uc_1_wrd),
    .AddrA(uc_1_addra), .AddrB(uc_1_addrb), .IMMED(uc_1_immed), .RbImm(uc_1_rbimm), .F(uc_1_f),
    .CmpAL(uc_1_cmpal), .CLK(clock_1_out), .DATAOUT(DATAOUT), .z(upgsmall_1_z));
endmodule
