// Logisim project Ejercicio5.circ as structural Verilog: 5 circuits, main circuit UPGSmall
module UPGSmall (
  input  [7:0] DATAIN,
  input  InALU,
  input  CLK,
  input  [2:0] AddrD,
  input  reset,
  input  WrD,
  input  [2:0] AddrB,
  input  [2:0] AddrA,
  input  [7:0] IMMED,
  input  ImRb,
  input  [1:0] F,
  output [7:0] DATAOUT,
  output z
);

  wire [7:0] alu_1_w, multiplexer_1_out, multiplexer_2_out, regfile_1_a;

  Multiplexer #(.width(8)) multiplexer_1 (.in0(DATAIN), .in1(alu_1_w), .out(multiplexer_1_out), .sel(InALU));
  RegFile regfile_1 (
    .clk(CLK), .WrD(WrD), .AddrD(AddrD), .D(multiplexer_1_out), .Reset(reset), .AddrB(AddrB), .AddrA(AddrA),
    .A(regfile_1_a), .B(DATAOUT));
  Multiplexer #(.width(8)) multiplexer_2 (.in0(IMMED), .in1(DATAOUT), .out(multiplexer_2_out), .sel(ImRb));
  ALU alu_1 (.A(regfile_1_a), .B(multiplexer_2_out), .F(F), .z(z), .W(alu_1_w));
endmodule

module RegFile (
  input  [7:0] D,
  input  WrD,
  input  [2:0] AddrD,
  input  clk,
  input  Reset,
  input  [2:0] AddrB,
  input  [2:0] AddrA,
  output [7:0] A,
  output [7:0] B
);

  wire decoder_1_out0, decoder_1_out1, decoder_1_out2, decoder_1_out3, decoder_1_out4, decoder_1_out5,
       decoder_1_out6, decoder_1_out7;
  wire [7:0] register_1_q, register_2_q, register_3_q, register_4_q, register_5_q, register_6_q,
       register_7_q, register_8_q;

  Decoder #(.select(3)) decoder_1 (
    .out0(decoder_1_out0), .out1(decoder_1_out1), .out2(decoder_1_out2), .out3(decoder_1_out3),
    .out4(decoder_1_out4), .out5(decoder_1_out5), .out6(decoder_1_out6), .out7(decoder_1_out7), .sel(AddrD),
    .en(WrD));
  Register register_1 (.D(D), .en(decoder_1_out0), .clk(clk), .Q(register_1_q), .clr(Reset));
  Register register_2 (.D(D), .en(decoder_1_out1), .clk(clk), .Q(register_2_q), .clr(Reset));
  Register register_3 (.D(D), .en(decoder_1_out2), .clk(clk), .Q(register_3_q), .clr(Reset));
  Register register_4 (.D(D), .en(decoder_1_out3), .clk(clk), .Q(register_4_q), .clr(Reset));
  Register register_5 (.D(D), .en(decoder_1_out4), .clk(clk), .Q(register_5_q), .clr(Reset));
  Register register_6 (.D(D), .en(decoder_1_out5), .clk(clk), .Q(register_6_q), .clr(Reset));
  Register register_7 (.D(D), .en(decoder_1_out6), .clk(clk), .Q(register_7_q), .clr(Reset));
  Register register_8 (.D(D), .en(decoder_1_out7), .clk(clk), .Q(register_8_q), .clr(Reset));
  Multiplexer #(.select(3), .width(8)) multiplexer_1 (
    .in0(register_1_q), .in1(register_2_q), .in2(register_3_q), .in3(register_4_q), .in4(register_5_q),
    .in5(register_6_q), .in6(register_7_q), .in7(register_8_q), .out(B), .sel(AddrB));
  Multiplexer #(.select(3), .width(8)) multiplexer_2 (
    .in0(register_1_q), .in1(register_2_q), .in2(register_3_q), .in3(register_4_q), .in4(register_5_q),
    .in5(register_6_q), .in6(register_7_q), .in7(register_8_q), .out(A), .sel(AddrA));
endmodule

module ALU (
  input  [7:0] A,
  input  [7:0] B,
  input  [1:0] F,
  output [7:0] W,
  output z
);

  wire [7:0] adder_1_out, and_1_out, not_1_out, xor_1_out;

  assign not_1_out = ~A;  // NOT_Gate not_1, 8 bits wide
  assign and_1_out = B & A;  // AND_Gate and_1, 8 bits wide
  assign xor_1_out = B ^ A;  // XOR_Gate xor_1, 8 bits wide
  Adder adder_1 (.a(B), .b(A), .out(adder_1_out));  // open: cin, cout
  Multiplexer #(.select(2), .width(8)) multiplexer_1 (
    .in0(not_1_out), .in1(and_1_out), .in2(xor_1_out), .in3(adder_1_out), .out(W), .sel(F));
  Comparator comparator_1 (.a(W), .b({8{1'b0}}), .eq(z));  // open: gt, lt
endmodule

module UC (
  input  z,
  input  reset,
  input  CLK,
  output [7:0] IMMED,
  output InALU,
  output WrD,
  output [2:0] AddrB,
  output [2:0] AddrA,
  output [2:0] AddrD,
  output ImRb,
  output [1:0] F
);

  wire [1:0] register_1_q, rom_1_data;

  ROM #(.addrWidth(3), .dataWidth(2)) rom_1 (.addr({register_1_q, z}), .data(rom_1_data));
  Register #(.width(2)) register_1 (.D(rom_1_data), .en(1'b1), .clk(CLK), .Q(register_1_q), .clr(reset));
  ROM #(.addrWidth(2), .dataWidth(22)) rom_2 (
    .addr(register_1_q), .data({F, ImRb, AddrD, AddrA, AddrB, WrD, InALU, IMMED}));

  // Notes on the sheet:
  //   contents of rom_1 (hex, n*v repeats v):
  //   1 1 2 5*3
  //   contents of rom_2 (hex, n*v repeats v):
  //   20200 134301 324301 800
endmodule

module solucion (
  input  [7:0] DATAIN,
  input  reset,
  output [7:0] DATAOUT
);

  wire CLK_out, uc_1_imrb, uc_1_inalu, uc_1_wrd, upgsmall_1_z;
  wire [1:0] uc_1_f;
  wire [2:0] uc_1_addra, uc_1_addrb, uc_1_addrd;
  wire [7:0] uc_1_immed;

  Clock CLK (.out(CLK_out));
  UC uc_1 (
    .z(upgsmall_1_z), .reset(reset), .CLK(CLK_out), .IMMED(uc_1_immed), .InALU(uc_1_inalu), .WrD(uc_1_wrd),
    .AddrB(uc_1_addrb), .AddrA(uc_1_addra), .AddrD(uc_1_addrd), .ImRb(uc_1_imrb), .F(uc_1_f));
  UPGSmall upgsmall_1 (
    .DATAIN(DATAIN), .InALU(uc_1_inalu), .CLK(CLK_out), .AddrD(uc_1_addrd), .reset(reset), .WrD(uc_1_wrd),
    .AddrB(uc_1_addrb), .AddrA(uc_1_addra), .IMMED(uc_1_immed), .ImRb(uc_1_imrb), .F(uc_1_f),
    .DATAOUT(DATAOUT), .z(upgsmall_1_z));
endmodule
