// Logisim project Ejercicio6.circ as structural Verilog
module UP (
  input  [3:0] w3,
  input  [3:0] w2,
  input  [3:0] w1,
  input  InAU,
  input  [3:0] w0,
  input  [1:0] selector,
  input  WrD,
  input  CLK,
  input  reset,
  output [3:0] DATAOUT
);

  wire [3:0] adder_1_out, multiplexer_1_out, multiplexer_2_out;

  Multiplexer #(.select(2), .width(4)) multiplexer_1 (
    .in0(w0), .in1(w1), .in2(w2), .in3(w3), .out(multiplexer_1_out), .sel(selector));
  Multiplexer #(.width(4)) multiplexer_2 (.in0(4'b0000), .in1(adder_1_out), .out(multiplexer_2_out), .sel(InAU));
  Register #(.width(4)) register_1 (.D(multiplexer_2_out), .en(WrD), .clk(CLK), .Q(DATAOUT), .clr(reset));
  Adder #(.width(4)) adder_1 (.a(multiplexer_1_out), .b(DATAOUT), .out(adder_1_out));  // open: cin, cout
endmodule

module UC (
  input  CLK,
  input  reset,
  output WrD,
  output InAU,
  output [1:0] selector,
  output FIN
);

  wire not_1_out, not_2_out;
  wire [2:0] register_1_q, rom_1_data;

  ROM #(.addrWidth(3), .dataWidth(3)) rom_1 (.addr(register_1_q), .data(rom_1_data));
  Register #(.width(3)) register_1 (.D(rom_1_data), .en(1'b1), .clk(CLK), .Q(register_1_q), .clr(reset));
  ROM #(.addrWidth(3), .dataWidth(4)) rom_2 (.addr(register_1_q), .data({selector, InAU, WrD}));
  not not_1 (not_1_out, register_1_q[0]);
  not not_2 (not_2_out, register_1_q[1]);
  and and_1 (FIN, not_1_out, not_2_out, register_1_q[2]);

  // Notes on the sheet:
  //   contents of rom_1 (hex, n*v repeats v):
  //   1 2 3 4 4
  //   contents of rom_2 (hex, n*v repeats v):
  //   3 7 b f
endmodule

module UPG (
  input  [3:0] w3,
  input  [3:0] w2,
  input  [3:0] w1,
  input  [3:0] w0,
  input  CLK,
  input  reset,
  output [3:0] salida,
  output FIN
);

  wire uc_1_inau, uc_1_wrd;
  wire [1:0] uc_1_selector;

  UC uc_1 (.CLK(CLK), .reset(reset), .WrD(uc_1_wrd), .InAU(uc_1_inau), .selector(uc_1_selector), .FIN(FIN));
  UP up_1 (
    .w3(w3), .w2(w2), .w1(w1), .InAU(uc_1_inau), .w0(w0), .selector(uc_1_selector), .WrD(uc_1_wrd),
    .CLK(CLK), .reset(reset), .DATAOUT(salida));
endmodule

module activacion (
  input  [3:0] w,
  output [3:0] salida
);

  Multiplexer #(.width(4)) multiplexer_1 (.in0(w), .in1(4'b0000), .out(salida), .sel(w[3]));
endmodule

module solucion (
  input  [3:0] w3,
  input  [3:0] w2,
  input  [3:0] w1,
  input  [3:0] w0,
  input  reset,
  output [3:0] out_6
);

  wire clock_1_out, upg_1_fin;
  wire [3:0] multiplexer_1_out, upg_1_salida;

  Clock clock_1 (.out(clock_1_out));
  UPG upg_1 (
    .w3(w3), .w2(w2), .w1(w1), .w0(w0), .CLK(clock_1_out), .reset(reset), .salida(upg_1_salida),
    .FIN(upg_1_fin));
  Multiplexer #(.width(4)) multiplexer_1 (.in0(4'b0000), .in1(upg_1_salida), .out(multiplexer_1_out), .sel(upg_1_fin));
  activacion activacion_1 (.w(multiplexer_1_out), .salida(out_6));
endmodule
