// Logisim project Ejercicio7.circ as structural Verilog: 3 circuits, main circuit UPGSmall
module UPGSmall (
  input  [7:0] DATAIN,
  input  InALU,
  input  Reset,
  input  [1:0] AddrD,
  input  WrD,
  input  [1:0] AddrA,
  input  [1:0] AddrB,
  input  [3:0] IMMED,
  input  RbImm,
  input  [1:0] F,
  input  CmpAL,
  output [7:0] DATAOUT,
  output z
);

  wire clock_1_out;
  wire [7:0] alu_1_w, bit_extender_1_out, multiplexer_1_out, multiplexer_2_out, regfile_1_a;

  Clock clock_1 (.out(clock_1_out));
  assign bit_extender_1_out = {{4{IMMED[3]}}, IMMED};  // Bit_Extender bit_extender_1
  Multiplexer #(.width(8)) multiplexer_1 (.in0(DATAIN), .in1(alu_1_w), .out(multiplexer_1_out), .sel(InALU));
  RegFile regfile_1 (
    .clk(clock_1_out), .WrD(WrD), .AddrD(AddrD), .D(multiplexer_1_out), .Reset(Reset), .AddrB(AddrB),
    .AddrA(AddrA), .A(regfile_1_a), .B(DATAOUT));
  Multiplexer #(.width(8)) multiplexer_2 (
    .in0(bit_extender_1_out), .in1(DATAOUT), .out(multiplexer_2_out), .sel(RbImm));
  ALU alu_1 (.CmpAL(CmpAL), .A(regfile_1_a), .B(multiplexer_2_out), .F(F), .z(z), .W(alu_1_w));
endmodule

module RegFile (
  input  [7:0] D,
  input  WrD,
  input  [1:0] AddrD,
  input  clk,
  input  Reset,
  input  [1:0] AddrB,
  input  [1:0] AddrA,
  output [7:0] A,
  output [7:0] B
);

  wire decoder_1_out0, decoder_1_out1, decoder_1_out2, decoder_1_out3;
  wire [7:0] register_1_q, register_2_q, register_3_q, register_4_q;

  Decoder #(.select(2)) decoder_1 (
    .out0(decoder_1_out0), .out1(decoder_1_out1), .out2(decoder_1_out2), .out3(decoder_1_out3), .sel(AddrD),
    .en(WrD));
  Register register_1 (.D(D), .en(decoder_1_out0), .clk(clk), .Q(register_1_q), .clr(Reset));
  Register register_2 (.D(D), .en(decoder_1_out1), .clk(clk), .Q(register_2_q), .clr(Reset));
  Register register_3 (.D(D), .en(decoder_1_out2), .clk(clk), .Q(register_3_q), .clr(Reset));
  Register register_4 (.D(D), .en(decoder_1_out3), .clk(clk), .Q(register_4_q), .clr(Reset));
  Multiplexer #(.select(2), .width(8)) multiplexer_1 (
    .in0(register_1_q), .in1(register_2_q), .in2(register_3_q), .in3(register_4_q), .out(B), .sel(AddrB));
  Multiplexer #(.select(2), .width(8)) multiplexer_2 (
    .in0(register_1_q), .in1(register_2_q), .in2(register_3_q), .in3(register_4_q), .out(A), .sel(AddrA));
endmodule

module ALU (
  input  [7:0] A,
  input  [7:0] B,
  input  [1:0] F,
  input  CmpAL,
  output [7:0] W,
  output z
);

  wire comparator_1_eq, comparator_1_lt, or_1_out;
  wire [7:0] adder_1_out, and_1_out, bit_extender_1_out, bit_extender_2_out, bit_extender_3_out, not_1_out,
       xor_1_out;

  assign not_1_out = ~A;  // NOT_Gate not_1, 8 bits wide
  assign and_1_out = A & B;  // AND_Gate and_1, 8 bits wide
  Adder adder_1 (.a(A), .b(B), .out(adder_1_out), .cin(1'b0));  // open: cout
  assign xor_1_out = A ^ B;  // XOR_Gate xor_1, 8 bits wide
  Comparator comparator_1 (.a(A), .b(B), .eq(comparator_1_eq), .lt(comparator_1_lt));  // open: gt
  or or_1 (or_1_out, comparator_1_lt, comparator_1_eq);
  assign bit_extender_1_out = {{7{1'b0}}, comparator_1_eq};  // Bit_Extender bit_extender_1
  assign bit_extender_2_out = {{7{1'b0}}, or_1_out};  // Bit_Extender bit_extender_2
  assign bit_extender_3_out = {{7{1'b0}}, comparator_1_lt};  // Bit_Extender bit_extender_3
  Multiplexer #(.select(3), .width(8)) multiplexer_1 (
    .in0(not_1_out), .in1(and_1_out), .in2(adder_1_out), .in3(xor_1_out), .in4(bit_extender_1_out),
    .in5(bit_extender_2_out), .in6(bit_extender_3_out), .in7(B), .out(W), .sel({CmpAL, F}));
  Comparator comparator_2 (.a(W), .b({8{1'b0}}), .eq(z));  // open: gt, lt
endmodule
