// Logisim project Ejercicio9.circ as structural Verilog: 5 circuits, main circuit UPGSmall
module UPGSmall (
  input  [7:0] DATAIN,
  input  AddrD,
  input  Reset,
  input  WrD,
  input  AddrB,
  input  AddrA,
  input  [1:0] F,
  input  CmpAL,
  input  R0_R1,
  input  clk,
  output [7:0] DATAOUT,
  output z
);

  wire demultiplexer_1_out0, demultiplexer_1_out1;
  wire [7:0] alu_1_w, regfile_1_a;

  Demultiplexer demultiplexer_1 (.out0(demultiplexer_1_out0), .out1(demultiplexer_1_out1), .in(WrD), .sel(R0_R1));
  RegFile regfile_1 (
    .clk(clk), .WrD(demultiplexer_1_out0), .AddrD(AddrD), .D(DATAIN), .Reset(Reset), .AddrA(AddrA),
    .A(regfile_1_a));
  RegFile regfile_2 (
    .clk(clk), .WrD(demultiplexer_1_out1), .AddrD(AddrD), .D(alu_1_w), .Reset(Reset), .AddrA(AddrB),
    .A(DATAOUT));
  ALU alu_1 (.CmpAL(CmpAL), .A(regfile_1_a), .B(DATAOUT), .F(F), .z(z), .W(alu_1_w));
endmodule

module RegFile (
  input  [7:0] D,
  input  WrD,
  input  AddrD,
  input  clk,
  input  Reset,
  input  AddrA,
  output [7:0] A
);

  wire decoder_1_out0, decoder_1_out1;
  wire [7:0] register_1_q, register_2_q;

  Decoder decoder_1 (.out0(decoder_1_out0), .out1(decoder_1_out1), .sel(AddrD), .en(WrD));
  Register register_1 (.D(D), .en(decoder_1_out0), .clk(clk), .Q(register_1_q), .clr(Reset));
  Register register_2 (.D(D), .en(decoder_1_out1), .clk(clk), .Q(register_2_q), .clr(Reset));
  Multiplexer #(.width(8)) multiplexer_1 (.in0(register_1_q), .in1(register_2_q), .out(A), .sel(AddrA));
endmodule

module ALU (
  input  [7:0] A,
  input  [7:0] B,
  input  [1:0] F,
  input  CmpAL,
  output [7:0] W,
  output z
);

  wire comparator_1_eq, comparator_1_lt, or_1_out;
  wire [7:0] adder_1_out, and_1_out, bit_extender_1_out, bit_extender_2_out, bit_extender_3_out,
       multiplexer_1_out, multiplexer_2_out, not_1_out, xor_1_out;

  assign not_1_out = ~A;  // NOT_Gate not_1, 8 bits wide
  assign and_1_out = B & A;  // AND_Gate and_1, 8 bits wide
  assign xor_1_out = B ^ A;  // XOR_Gate xor_1, 8 bits wide
  Adder adder_1 (.a(B), .b(A), .out(adder_1_out));  // open: cin, cout
  Comparator comparator_1 (.a(B), .b(A), .eq(comparator_1_eq), .lt(comparator_1_lt));  // open: gt
  or or_1 (or_1_out, comparator_1_eq, comparator_1_lt);
  assign bit_extender_1_out = {{7{1'b0}}, or_1_out};  // Bit_Extender bit_extender_1
  assign bit_extender_2_out = {{7{1'b0}}, comparator_1_lt};  // Bit_Extender bit_extender_2
  assign bit_extender_3_out = {{7{1'b0}}, comparator_1_eq};  // Bit_Extender bit_extender_3
  Multiplexer #(.select(2), .width(8)) multiplexer_1 (
    .in0(not_1_out), .in1(and_1_out), .in2(xor_1_out), .in3(adder_1_out), .out(multiplexer_1_out), .sel(F));
  Multiplexer #(.select(2), .width(8)) multiplexer_2 (
    .in0(bit_extender_1_out), .in1(bit_extender_2_out), .in2(bit_extender_3_out), .in3(B),
    .out(multiplexer_2_out), .sel(F));
  Multiplexer #(.width(8)) multiplexer_3 (.in0(multiplexer_1_out), .in1(multiplexer_2_out), .out(W), .sel(CmpAL));
  Comparator comparator_2 (.a(W), .b({8{1'b0}}), .eq(z));  // open: gt, lt
endmodule

module UC (
  input  CLK,
  input  reset,
  output AddrB,
  output AddrA,
  output AddrD,
  output WrD,
  output R0_R1,
  output [1:0] F,
  output CmpAL
);

  wire [1:0] PC_q, rom_1_data;

  ROM #(.addrWidth(2), .dataWidth(2)) rom_1 (.addr(PC_q), .data(rom_1_data));
  Register #(.width(2)) PC (.D(rom_1_data), .en(1'b1), .clk(CLK), .Q(PC_q), .clr(reset));
  ROM #(.addrWidth(2)) rom_2 (.addr(PC_q), .data({CmpAL, F, R0_R1, WrD, AddrD, AddrA, AddrB}));

  // Notes on the sheet:
  //   contents of rom_1 (hex, n*v repeats v):
  //   1 2 2
  //   contents of rom_2 (hex, n*v repeats v):
  //   c 7b
endmodule

module solucion (
  input  [7:0] DATAIN,
  input  reset,
  output [7:0] DATAOUT
);

  wire CLK_out, uc_1_addra, uc_1_addrb, uc_1_addrd, uc_1_cmpal, uc_1_r0_r1, uc_1_wrd;
  wire [1:0] uc_1_f;

  UC uc_1 (
    .CLK(CLK_out), .reset(reset), .AddrB(uc_1_addrb), .AddrA(uc_1_addra), .AddrD(uc_1_addrd), .WrD(uc_1_wrd),
    .R0_R1(uc_1_r0_r1), .F(uc_1_f), .CmpAL(uc_1_cmpal));
  Clock CLK (.out(CLK_out));
  UPGSmall upgsmall_1 (
    .DATAIN(DATAIN), .AddrD(uc_1_addrd), .Reset(reset), .WrD(uc_1_wrd), .AddrB(uc_1_addrb),
    .AddrA(uc_1_addra), .F(uc_1_f), .CmpAL(uc_1_cmpal), .R0_R1(uc_1_r0_r1), .clk(CLK_out), .DATAOUT(DATAOUT));  // open: z
endmodule
