// Logisim project bombonasAgua.circ as structural Verilog: 2 circuits, main circuit main
module main (
  input  E,
  input  F,
  output B1,
  output B0
);

  wire and_1_out, and_2_out, and_3_out, and_4_out, and_5_out, and_6_out, and_7_out, and_8_out, and_9_out,
       and_10_out, and_11_out, and_12_out, and_13_out, and_14_out, clock_1_out, lastUsed_q, not_1_out,
       not_2_out, not_3_out, or_1_out, or_2_out, or_3_out, or_4_out, or_7_out;

  not not_1 (not_1_out, E);
  not not_2 (not_2_out, F);
  not not_3 (not_3_out, lastUsed_q);
  D_Flip_Flop lastUsed (.D(or_7_out), .clk(clock_1_out), .Q(lastUsed_q));  // open: Qn, preset, reset
  Clock clock_1 (.out(clock_1_out));
  and and_1 (and_1_out, not_1_out, not_2_out);
  and and_2 (and_2_out, and_1_out, lastUsed_q);
  and and_3 (and_3_out, not_1_out, F);
  and and_4 (and_4_out, and_3_out, not_3_out);
  and and_5 (and_5_out, E, not_2_out);
  and and_6 (and_6_out, and_5_out, not_3_out);
  and and_7 (and_7_out, E, F);
  and and_8 (and_8_out, and_7_out, lastUsed_q);
  and and_9 (and_9_out, not_1_out, not_2_out);
  or or_1 (or_1_out, and_9_out, and_10_out);
  and and_10 (and_10_out, not_1_out, not_3_out);
  and and_11 (and_11_out, not_2_out, not_3_out);
  and and_12 (and_12_out, not_1_out, not_2_out);
  or or_2 (or_2_out, and_12_out, and_13_out);
  and and_13 (and_13_out, not_1_out, lastUsed_q);
  and and_14 (and_14_out, not_2_out, lastUsed_q);
  or or_3 (or_3_out, and_2_out, and_4_out);
  or or_4 (or_4_out, and_6_out, and_8_out);
  or or_5 (B1, or_1_out, and_11_out);
  or or_6 (B0, or_2_out, and_14_out);
  or or_7 (or_7_out, or_3_out, or_4_out);
endmodule

module conROM (
  input  E,
  input  F,
  input  Q,
  output Qp,
  output B1,
  output B0
);

  ROM #(.addrWidth(3), .dataWidth(3)) rom_1 (.addr({E, F, Q}), .data({B0, B1, Qp}));

  // Notes on the sheet:
  //   contents of rom_1 (hex, n*v repeats v):
  //   6 7 3 4 3 4 0 1
endmodule
