// Logisim project ejercicio1.circ as structural Verilog: 4 circuits, main circuit main
module main (
  input  [2:0] X,
  output isPrimo
);

  wire and_1_out, and_2_out, not_1_out;

  not not_1 (not_1_out, X[2]);
  and and_1 (and_1_out, X[1], not_1_out);
  and and_2 (and_2_out, X[0], X[2]);
  or or_1 (isPrimo, and_1_out, and_2_out);
endmodule

module cuadrado (
  input  [2:0] X,
  output [4:0] cuadr
);

  wire and_1_out, and_2_out, and_3_out, and_4_out, not_1_out, not_2_out, not_3_out;

  not not_1 (not_1_out, X[0]);
  not not_2 (not_2_out, X[1]);
  not not_3 (not_3_out, X[2]);
  and and_1 (and_1_out, X[0], not_3_out);
  and and_2 (and_2_out, X[0], X[2]);
  and and_3 (and_3_out, not_3_out, X[1], X[0]);
  and and_4 (and_4_out, X[2], not_2_out, X[0]);
  or or_1 (cuadr[0], and_1_out, and_2_out);
  and and_5 (cuadr[2], X[1], not_1_out);
  or or_2 (cuadr[3], and_3_out, and_4_out);
  and and_6 (cuadr[4], not_2_out, not_1_out, X[2]);

  assign cuadr[1] = 1'b0;
endmodule

module pow_pri (
  input  [2:0] in_1,
  output isPrimo,
  output [4:0] cuadr
);

  main main_1 (.X(in_1), .isPrimo(isPrimo));
  cuadradoROM cuadradorom_1 (.X(in_1), .cuadr(cuadr));
endmodule

module cuadradoROM (
  input  [2:0] X,
  output [4:0] cuadr
);

  ROM #(.addrWidth(3), .dataWidth(5)) rom_1 (.addr(X), .data(cuadr));

  // Notes on the sheet:
  //   contents of rom_1 (hex, n*v repeats v):
  //   0 1 4 9 10 9 4 1
endmodule
