// Logisim project ejercicio10.circ as structural Verilog: 1 circuit, main circuit circuito
module circuito (
  input  c2,
  input  c1,
  input  c0,
  output T0,
  output T1,
  output T2
);

  wire and_1_out, and_2_out, and_3_out, and_4_out, and_5_out, and_6_out, and_7_out, and_8_out, and_9_out,
       not_1_out, not_2_out, not_3_out, or_2_out;

  not not_1 (not_1_out, c2);
  not not_2 (not_2_out, c1);
  not not_3 (not_3_out, c0);
  and and_1 (and_1_out, c1, not_3_out);
  and and_2 (and_2_out, c2, c1);
  and and_3 (and_3_out, not_1_out, not_2_out);
  and and_4 (and_4_out, not_1_out, c1);
  and and_5 (and_5_out, c1, c0);
  or or_1 (T0, and_1_out, and_2_out);
  and and_6 (and_6_out, and_3_out, c0);
  or or_2 (or_2_out, and_6_out, and_7_out);
  and and_7 (and_7_out, and_4_out, not_3_out);
  and and_8 (and_8_out, c2, c1);
  and and_9 (and_9_out, and_8_out, c0);
  or or_3 (T2, and_5_out, c2);
  or or_4 (T1, or_2_out, and_9_out);
endmodule
