// Logisim project ejercicio11.circ as structural Verilog: 1 circuit, main circuit main
module main (
  input  M1,
  input  M2,
  input  M3,
  output wOUT,
  output C0,
  output C1
);

  wire and_1_out, and_2_out, and_3_out, and_4_out, and_5_out, and_6_out, and_7_out, not_1_out, not_2_out,
       not_3_out;

  not not_1 (not_1_out, M1);
  not not_2 (not_2_out, M2);
  not not_3 (not_3_out, M3);
  and and_1 (and_1_out, M2, M3);
  and and_2 (and_2_out, M1, M3);
  and and_3 (and_3_out, M1, M2);
  and and_4 (and_4_out, not_1_out, M3);
  and and_5 (and_5_out, M1, not_3_out);
  and and_6 (and_6_out, not_2_out, M3);
  and and_7 (and_7_out, M2, not_3_out);
  or or_1 (wOUT, and_1_out, and_2_out, and_3_out);
  or or_2 (C0, and_4_out, and_5_out);
  or or_3 (C1, and_6_out, and_7_out);
endmodule
