// Logisim project ejercicio12.circ as structural Verilog
module main (
  input  [3:0] X,
  input  [3:0] Y,
  output OvBN,
  output [3:0] W
);

  wire romcmp_1_z;
  wire [3:0] adder_1_out;

  Adder #(.width(4)) adder_1 (.a(X), .b(Y), .out(adder_1_out), .cin(1'b0), .cout(OvBN));
  ROMCMP romcmp_1 (.in_1(X), .Z(romcmp_1_z));
  Multiplexer #(.width(4)) multiplexer_1 (.in0(adder_1_out), .in1(Y), .out(W), .sel(romcmp_1_z));
endmodule

module ROMCMP (
  input  [3:0] in_1,
  output Z
);

  ROM #(.addrWidth(4), .dataWidth(1)) rom_1 (.addr(in_1));  // open: data

  // Notes on the sheet:
  //   contents of rom_1 (hex, n*v repeats v):
  //   1
endmodule
