// Logisim project ejercicio13.circ as structural Verilog
module CondAdder (
  input  [3:0] X,
  input  [3:0] Y,
  input  [3:0] Z,
  output [3:0] W
);

  wire adder_1_cout, adder_2_cout;
  wire [3:0] adder_1_out, adder_2_out, negator_1_out;

  // NoConnect on adder_1_cout
  // NoConnect on adder_2_cout
  Negator #(.width(4)) negator_1 (.in(Y), .out(negator_1_out));
  Adder #(.width(4)) adder_1 (.a(X), .b(Y), .out(adder_1_out), .cin(1'b0), .cout(adder_1_cout));
  Adder #(.width(4)) adder_2 (.a(X), .b(negator_1_out), .out(adder_2_out), .cin(1'b0), .cout(adder_2_cout));
  Multiplexer #(.width(4)) multiplexer_1 (.in0(adder_1_out), .in1(adder_2_out), .out(W), .sel(Z[0]));

  // Notes on the sheet:
  //   Tp: 540 ut
  //   Inversor: 240 (FA) + 10 (Ca1) = 250ut
  //   FA (4): 60 + 20 + 20 + 40*2 + 60 = 240ut
  //   MUX (4): MUX(1) [PARALELO] = 50ut
endmodule
