// Logisim project ejercicio14.circ as structural Verilog: 3 circuits, main circuit main
module main (
  input  [3:0] X,
  output [3:0] ZigZag
);

  wire [3:0] adder_1_out, multiplexer_1_out, negator_1_out, shifter_1_out;

  Multiplexer #(.width(4)) multiplexer_1 (.in0(X), .in1(negator_1_out), .out(multiplexer_1_out), .sel(X[3]));
  Negator #(.width(4)) negator_1 (.in(X), .out(negator_1_out));
  Shifter #(.width(4)) shifter_1 (.in(multiplexer_1_out), .\dist (2'b01), .out(shifter_1_out));
  Adder #(.width(4)) adder_1 (.a(shifter_1_out), .b(4'b1111), .out(adder_1_out), .cin(1'b0));  // open: cout
  Multiplexer #(.width(4)) multiplexer_2 (.in0(shifter_1_out), .in1(adder_1_out), .out(ZigZag), .sel(X[3]));
endmodule

module circuito (
  input  [3:0] X,
  output [3:0] ZigZag
);

  wire and_1_out, and_2_out, and_3_out, and_4_out, and_5_out, and_6_out, not_1_out, not_2_out, not_3_out,
       not_4_out;

  not not_1 (not_1_out, X[3]);
  not not_2 (not_2_out, X[2]);
  not not_3 (not_3_out, X[1]);
  not not_4 (not_4_out, X[0]);
  and and_1 (and_1_out, not_1_out, X[2]);
  or or_1 (ZigZag[3], and_1_out, and_2_out);
  and and_2 (and_2_out, X[3], not_2_out);
  and and_3 (and_3_out, not_1_out, X[1]);
  or or_2 (ZigZag[2], and_3_out, and_4_out);
  and and_4 (and_4_out, X[3], not_3_out);
  and and_5 (and_5_out, not_1_out, X[0]);
  or or_3 (ZigZag[1], and_5_out, and_6_out);
  and and_6 (and_6_out, X[3], not_4_out);

  assign ZigZag[0] = X[3];
endmodule

module conROM (
  input  [3:0] X,
  output [3:0] ZigZag
);

  ROM #(.addrWidth(4), .dataWidth(4)) rom_1 (.addr(X), .data(ZigZag));

  // Notes on the sheet:
  //   contents of rom_1 (hex, n*v repeats v):
  //   0 2 4 6 8 a c e f d b 9 7 5 3 1
endmodule
