// Logisim project ejercicio19.circ as structural Verilog: 2 circuits, main circuit main
module main (
  input  siete,
  input  seis,
  input  cinco,
  input  cuatro,
  input  tres,
  input  dos,
  input  uno,
  input  B,
  input  [3:0] pisoActual,
  output [3:0] out_10
);

  wire [2:0] priority_encoder_1_out;

  Priority_Encoder priority_encoder_1 (
    .in0(B), .in1(uno), .in2(dos), .in3(tres), .in4(cuatro), .in5(cinco), .in6(seis), .in7(siete),
    .out(priority_encoder_1_out), .en_in(1'b1));  // open: gs, en_out
  Subtractor #(.width(4)) subtractor_1 (
    .a({1'b0, priority_encoder_1_out}), .b(pisoActual), .out(out_10));  // open: bin, bout
endmodule

module circuito (
  input  siete,
  input  seis,
  input  cinco,
  input  cuatro,
  input  tres,
  input  dos,
  input  uno,
  input  B,
  input  [3:0] pisoActual,
  output [3:0] x
);

  wire and_1_out, and_2_out, and_3_out, and_4_out, and_5_out, and_6_out, and_7_out, and_8_out, and_9_out,
       and_10_out, and_11_out, and_12_out, and_13_out, and_14_out, and_15_out, and_16_out, and_17_out,
       and_18_out, and_19_out, and_20_out, and_21_out, and_22_out, and_23_out, and_24_out, and_25_out,
       and_26_out, and_27_out, and_28_out, and_29_out, and_30_out, and_31_out, and_32_out, and_33_out,
       and_34_out, and_35_out, and_36_out, and_37_out, and_38_out, and_39_out, and_40_out, and_41_out,
       and_42_out, and_43_out, and_44_out, and_45_out, and_46_out, and_47_out, and_48_out, and_49_out,
       and_50_out, and_51_out, and_52_out, and_53_out, and_54_out, and_55_out, and_56_out, and_57_out,
       not_1_out, not_2_out, not_3_out, not_4_out, not_5_out, not_6_out, not_7_out, not_8_out, not_9_out,
       not_10_out, not_11_out;

  not not_1 (not_1_out, siete);
  not not_2 (not_2_out, seis);
  not not_3 (not_3_out, cinco);
  not not_4 (not_4_out, cuatro);
  not not_5 (not_5_out, tres);
  not not_6 (not_6_out, dos);
  not not_7 (not_7_out, uno);
  not not_8 (not_8_out, pisoActual[3]);
  not not_9 (not_9_out, pisoActual[2]);
  not not_10 (not_10_out, pisoActual[1]);
  not not_11 (not_11_out, pisoActual[0]);
  and and_1 (and_1_out, not_1_out, not_2_out, not_3_out, not_4_out, not_5_out, not_6_out, not_7_out, not_8_out, pisoActual[0]);
  and and_2 (and_2_out, not_1_out, not_2_out, not_3_out, not_4_out, not_5_out, not_6_out, not_8_out, pisoActual[1]);
  and and_3 (and_3_out, not_1_out, not_2_out, not_3_out, not_4_out, not_8_out, pisoActual[2]);
  and and_4 (and_4_out, pisoActual[3], not_9_out, not_10_out, not_11_out);
  and and_5 (and_5_out, uno, pisoActual[3], not_9_out, not_10_out);
  and and_6 (and_6_out, not_1_out, not_2_out, not_3_out, not_4_out, not_5_out, not_8_out, pisoActual[1], pisoActual[0]);
  and and_7 (and_7_out, dos, pisoActual[3], not_9_out, not_10_out);
  and and_8 (and_8_out, dos, pisoActual[3], not_9_out, not_11_out);
  and and_9 (and_9_out, tres, pisoActual[3], not_9_out);
  and and_10 (and_10_out, not_1_out, not_2_out, not_3_out, not_8_out, pisoActual[2], pisoActual[0]);
  and and_11 (and_11_out, not_1_out, not_2_out, not_8_out, pisoActual[2], pisoActual[1]);
  and and_12 (and_12_out, cuatro, pisoActual[3], not_9_out);
  and and_13 (and_13_out, cuatro, pisoActual[3], not_10_out, not_11_out);
  and and_14 (and_14_out, cinco, pisoActual[3], not_9_out);
  and and_15 (and_15_out, cinco, pisoActual[3], not_10_out);
  and and_16 (and_16_out, not_1_out, not_8_out, pisoActual[2], pisoActual[1], pisoActual[0]);
  and and_17 (and_17_out, seis, pisoActual[3], not_9_out);
  and and_18 (and_18_out, seis, pisoActual[3], not_10_out);
  and and_19 (and_19_out, seis, pisoActual[3], not_11_out);
  and and_20 (and_20_out, siete, pisoActual[3]);
  and and_21 (and_21_out, not_1_out, not_2_out, not_3_out, not_4_out, pisoActual[2], not_10_out, not_11_out);
  and and_22 (and_22_out, not_2_out, not_3_out, not_4_out, not_5_out, not_9_out, pisoActual[1], pisoActual[0]);
  and and_23 (and_23_out, cuatro, not_9_out, not_10_out, not_11_out);
  and and_24 (and_24_out, not_1_out, not_2_out, not_3_out, cuatro, pisoActual[2], pisoActual[0]);
  and and_25 (and_25_out, not_1_out, not_2_out, cuatro, pisoActual[2], pisoActual[1]);
  and and_26 (and_26_out, cinco, not_9_out, not_10_out);
  and and_27 (and_27_out, not_1_out, not_2_out, cinco, pisoActual[2], pisoActual[1]);
  and and_28 (and_28_out, not_1_out, seis, pisoActual[2], pisoActual[1], pisoActual[0]);
  and and_29 (and_29_out, seis, not_9_out, not_10_out);
  and and_30 (and_30_out, seis, not_9_out, not_11_out);
  and and_31 (and_31_out, siete, not_9_out);
  and and_32 (and_32_out, not_1_out, not_2_out, not_3_out, not_4_out, tres, pisoActual[2]);
  and and_33 (and_33_out, not_4_out, not_5_out, not_6_out, not_7_out, not_9_out, not_10_out, pisoActual[0]);
  and and_34 (and_34_out, not_2_out, not_3_out, not_4_out, not_5_out, not_6_out, not_9_out, pisoActual[1]);
  and and_35 (and_35_out, not_1_out, not_2_out, not_3_out, uno, pisoActual[2], not_10_out, pisoActual[0]);
  and and_36 (and_36_out, not_1_out, not_2_out, not_3_out, not_4_out, dos, pisoActual[2], not_10_out);
  and and_37 (and_37_out, not_1_out, not_2_out, dos, pisoActual[2], pisoActual[1], not_11_out);
  and and_38 (and_38_out, not_2_out, not_3_out, not_6_out, not_7_out, not_10_out, pisoActual[0]);
  and and_39 (and_39_out, not_1_out, not_2_out, not_5_out, not_6_out, pisoActual[1], not_11_out);
  and and_40 (and_40_out, not_3_out, not_4_out, dos, not_10_out, not_11_out);
  and and_41 (and_41_out, not_1_out, not_4_out, not_5_out, dos, pisoActual[1], pisoActual[0]);
  and and_42 (and_42_out, not_2_out, not_3_out, cuatro, not_10_out, pisoActual[0]);
  and and_43 (and_43_out, not_1_out, not_2_out, cuatro, pisoActual[1], not_11_out);
  and and_44 (and_44_out, not_1_out, not_2_out, cinco, pisoActual[1]);
  and and_45 (and_45_out, seis, not_10_out, not_11_out);
  and and_46 (and_46_out, not_1_out, seis, pisoActual[1], pisoActual[0]);
  and and_47 (and_47_out, siete, not_10_out);
  and and_48 (and_48_out, not_2_out, not_3_out, not_4_out, tres, not_10_out);
  and and_49 (and_49_out, not_1_out, not_4_out, not_5_out, uno, pisoActual[1], pisoActual[0]);
  and and_50 (and_50_out, not_1_out, not_3_out, not_5_out, not_7_out, pisoActual[0]);
  and and_51 (and_51_out, not_2_out, not_4_out, not_6_out, uno, not_11_out);
  and and_52 (and_52_out, not_1_out, not_3_out, not_5_out, dos, pisoActual[0]);
  and and_53 (and_53_out, not_2_out, not_4_out, tres, not_11_out);
  and and_54 (and_54_out, not_1_out, not_3_out, cuatro, pisoActual[0]);
  and and_55 (and_55_out, not_2_out, cinco, not_11_out);
  and and_56 (and_56_out, not_1_out, seis, pisoActual[0]);
  and and_57 (and_57_out, siete, not_11_out);
  or or_1 (x[2], and_21_out, and_22_out, and_23_out, and_24_out, and_25_out, and_26_out, and_27_out, and_28_out, and_29_out, and_30_out, and_31_out, and_32_out, and_33_out, and_34_out, and_35_out, and_36_out, and_37_out);
  or or_2 (x[1], and_38_out, and_39_out, and_40_out, and_41_out, and_42_out, and_43_out, and_44_out, and_45_out, and_46_out, and_47_out, and_48_out, and_49_out);
  or or_3 (x[0], and_50_out, and_51_out, and_52_out, and_53_out, and_54_out, and_55_out, and_56_out, and_57_out);
  or or_4 (x[3], and_1_out, and_2_out, and_3_out, and_4_out, and_5_out, and_6_out, and_7_out, and_8_out, and_9_out, and_10_out, and_11_out, and_12_out, and_13_out, and_14_out, and_15_out, and_16_out, and_17_out, and_18_out, and_19_out, and_20_out);
endmodule
