// Logisim project ejercicio2.circ as structural Verilog
module mux_4 (
  input  [3:0] X0,
  input  [3:0] X1,
  input  [3:0] X2,
  input  [3:0] X3,
  input  [1:0] SEL,
  output [3:0] W
);

  wire [3:0] multiplexer_1_out, multiplexer_3_out;

  Multiplexer #(.width(4)) multiplexer_1 (.in0(X0), .in1(X1), .out(multiplexer_1_out), .sel(SEL[0]));
  Multiplexer #(.width(4)) multiplexer_2 (.in0(multiplexer_1_out), .in1(multiplexer_3_out), .out(W), .sel(SEL[1]));
  Multiplexer #(.width(4)) multiplexer_3 (.in0(X2), .in1(X3), .out(multiplexer_3_out), .sel(SEL[0]));
endmodule
