// Logisim project ejercicio20.circ as structural Verilog: 2 circuits, main circuit main
module main (
  input  [3:0] X,
  output [3:0] out_2
);

  ROM #(.addrWidth(4), .dataWidth(4)) rom_1 (.addr(X), .data(out_2));

  // Notes on the sheet:
  //   contents of rom_1 (hex, n*v repeats v):
  //   0 1 2 3 4 5 6 7 0 f e d c b a 9
endmodule

module MUX_decoder (
  input  [3:0] X,
  output [3:0] out_2
);

  wire [3:0] main_1_out_2;

  main main_1 (.X(X), .out_2(main_1_out_2));
  Multiplexer #(.width(4)) multiplexer_1 (.in0(X), .in1(main_1_out_2), .out(out_2), .sel(X[3]));

  // Notes on the sheet:
  //   Tp(ROM)=100ut
  //   Dado que en el 80% (ej) el número no se verá afectado por la conversión
  //   podemos calcular el tiempo de propagación promedio por
  //   Tp_promedio = 40*.8 + 140 *.2 = 60ut
  //   Tp(MUX)=40ut
endmodule
