// Logisim project ejercicio21.circ as structural Verilog: 4 circuits, main circuit main
module main (
  input  [2:0] in_1,
  output [2:0] out_2
);

  wire [2:0] multiplexer_1_out;

  Multiplexer #(.width(3)) multiplexer_1 (
    .in0({in_1[1:0], in_1[2]}), .in1({in_1[1:0], in_1[2]}), .out(multiplexer_1_out), .sel(in_1[0]));
  Adder #(.width(3)) adder_1 (.a(multiplexer_1_out), .b(3'b001), .out(out_2), .cin(1'b0));  // open: cout
endmodule

module encriptadoROM (
  input  [2:0] X,
  output [2:0] S
);

  ROM #(.addrWidth(3), .dataWidth(3)) rom_1 (.addr(X), .data(S));

  // Notes on the sheet:
  //   contents of rom_1 (hex, n*v repeats v):
  //   1 3 5 7 2 4 6
endmodule

module desencriptadoROM (
  input  [2:0] X,
  output [2:0] S
);

  ROM #(.addrWidth(3), .dataWidth(3)) rom_1 (.addr(X), .data(S));

  // Notes on the sheet:
  //   contents of rom_1 (hex, n*v repeats v):
  //   7 0 4 1 5 2 6 3
endmodule

module prueba (
  input  [2:0] in_1,
  output [2:0] out_2
);

  wire [2:0] encriptadorom_1_s;

  encriptadoROM encriptadorom_1 (.X(in_1), .S(encriptadorom_1_s));
  desencriptadoROM desencriptadorom_1 (.X(encriptadorom_1_s), .S(out_2));
endmodule
