// Logisim project ejercicio4.circ as structural Verilog: 1 circuit, main circuit main
module main (
  input  X,
  input  S,
  output W0,
  output W1
);

  wire not_1_out;

  not not_1 (not_1_out, S);
  and and_1 (W0, X, not_1_out);
  and and_2 (W1, X, S);
endmodule
