// Logisim project ejercicio5.circ as structural Verilog: 2 circuits, main circuit main
module main (
  input  [7:0] X,
  input  [7:0] Y,
  input  E_V,
  output [3:0] v_0,
  output [7:0] esc,
  output [3:0] v_1,
  output ov
);

  wire adder_1_cout, adder_3_cout, and_1_out, not_1_out;
  wire [3:0] adder_1_out, adder_2_out, adder_3_out, multiplexer_1_out;

  not not_1 (not_1_out, E_V);
  Adder #(.width(4)) adder_1 (.a(X[3:0]), .b(Y[3:0]), .out(adder_1_out), .cout(adder_1_cout));  // open: cin
  Adder #(.width(4)) adder_2 (.a(X[7:4]), .b(Y[7:4]), .out(adder_2_out), .cin(1'b0));  // open: cout
  Adder #(.width(4)) adder_3 (.a(X[7:4]), .b(Y[7:4]), .out(adder_3_out), .cin(1'b1), .cout(adder_3_cout));
  Multiplexer #(.width(4)) multiplexer_1 (
    .in0(adder_2_out), .in1(adder_3_out), .out(multiplexer_1_out), .sel(and_1_out));
  and and_1 (and_1_out, adder_1_cout, E_V);
  overflow overflow_1 (.Cout2(adder_3_cout), .Cout1(adder_1_cout), .CoutE(adder_3_cout), .E_V(E_V), .out_5(ov));
  Multiplexer #(.width(4)) multiplexer_2 (.in0(4'b0000), .in1(adder_1_out), .out(v_0), .sel(not_1_out));
  Multiplexer #(.width(4)) multiplexer_3 (.in0(4'b0000), .in1(multiplexer_1_out), .out(v_1), .sel(not_1_out));
  Multiplexer #(.width(8)) multiplexer_4 (
    .in0({multiplexer_1_out, adder_1_out}), .in1({8{1'b0}}), .out(esc), .sel(not_1_out));

  // Notes on the sheet:
  //   1 si es escalar
  //   La salida será cero en los vectores si se realiza una operación escalar
  //   y será cero en la escalar cuando se realice operación vectorial
endmodule

module overflow (
  input  Cout2,
  input  Cout1,
  input  CoutE,
  input  E_V,
  output out_5
);

  ROM #(.addrWidth(4), .dataWidth(1)) rom_1 (.addr({E_V, CoutE, Cout1, Cout2}));  // open: data

  // Notes on the sheet:
  //   contents of rom_1 (hex, n*v repeats v):
  //   0 1 1 1 0 1 1 1 4*0 4*1
endmodule
