// Logisim project ejercicio6.circ as structural Verilog: 3 circuits, main circuit main
module main (
  input  [3:0] in_1,
  output [3:0] W
);

  wire [3:0] shifter_1_out;

  Shifter #(.shift("ar"), .width(4)) shifter_1 (.in(in_1), .\dist (2'b01), .out(shifter_1_out));
  Multiplexer #(.width(4)) multiplexer_1 (.in0(in_1), .in1(shifter_1_out), .out(W), .sel(in_1[3]));

  // Notes on the sheet:
  //   El número es negativo
endmodule

module conROM (
  input  [3:0] in_1,
  output [3:0] out_2
);

  ROM #(.addrWidth(4), .dataWidth(4)) rom_1 (.addr(in_1), .data(out_2));

  // Notes on the sheet:
  //   contents of rom_1 (hex, n*v repeats v):
  //   0 1 2 3 4 5 6 7 c c d d e e f f
endmodule

module circuito (
  input  [3:0] a,
  output [3:0] W
);

  wire and_1_out, and_2_out, and_3_out, and_4_out, not_1_out;

  not not_1 (not_1_out, a[3]);
  or or_1 (W[2], a[2], a[3]);
  and and_1 (and_1_out, not_1_out, a[1]);
  or or_2 (W[1], and_1_out, and_2_out);
  and and_2 (and_2_out, a[3], a[2]);
  and and_3 (and_3_out, not_1_out, a[0]);
  or or_3 (W[0], and_3_out, and_4_out);
  and and_4 (and_4_out, a[3], a[1]);

  assign W[3] = a[3];
endmodule
