// Logisim project ejercicio7.circ as structural Verilog: 3 circuits, main circuit main
module main (
  input  [2:0] in_1,
  input  [1:0] in_2,
  output [2:0] out_3
);

  wire [1:0] multiplexer_1_out, negator_1_out;
  wire [2:0] shifter_1_out, shifter_2_out;

  Negator #(.width(2)) negator_1 (.in(in_2), .out(negator_1_out));
  Multiplexer #(.width(2)) multiplexer_1 (.in0(in_2), .in1(negator_1_out), .out(multiplexer_1_out), .sel(in_2[1]));
  Shifter #(.width(3)) shifter_1 (.in(in_1), .\dist (multiplexer_1_out), .out(shifter_1_out));
  Shifter #(.shift("lr"), .width(3)) shifter_2 (.in(in_1), .\dist (multiplexer_1_out), .out(shifter_2_out));
  Multiplexer #(.width(3)) multiplexer_2 (.in0(shifter_1_out), .in1(shifter_2_out), .out(out_3), .sel(in_2[1]));
endmodule

module circuito (
  input  [2:0] a,
  input  [1:0] b,
  output [2:0] x
);

  wire and_1_out, and_2_out, and_3_out, and_4_out, and_5_out, and_6_out, and_7_out, and_8_out, and_9_out,
       and_10_out, and_11_out, and_12_out, and_13_out, and_14_out, and_15_out, and_16_out, not_1_out,
       not_2_out, or_2_out, or_4_out;

  not not_1 (not_1_out, b[1]);
  not not_2 (not_2_out, b[0]);
  and and_1 (and_1_out, a[2], not_1_out);
  and and_2 (and_2_out, a[1], not_1_out);
  and and_3 (and_3_out, a[2], b[1]);
  and and_4 (and_4_out, a[0], not_1_out);
  and and_5 (and_5_out, a[2], b[1]);
  and and_6 (and_6_out, a[0], not_1_out);
  and and_7 (and_7_out, and_1_out, not_2_out);
  and and_8 (and_8_out, and_2_out, b[0]);
  and and_9 (and_9_out, and_3_out, b[0]);
  and and_10 (and_10_out, and_4_out, b[0]);
  and and_11 (and_11_out, a[1], not_1_out);
  and and_12 (and_12_out, and_5_out, not_2_out);
  and and_13 (and_13_out, and_6_out, not_2_out);
  and and_14 (and_14_out, a[1], b[1]);
  or or_1 (x[2], and_7_out, and_8_out);
  or or_2 (or_2_out, and_9_out, and_10_out);
  or or_3 (x[1], or_2_out, and_15_out);
  and and_15 (and_15_out, and_11_out, not_2_out);
  or or_4 (or_4_out, and_12_out, and_13_out);
  or or_5 (x[0], or_4_out, and_16_out);
  and and_16 (and_16_out, and_14_out, b[0]);
endmodule

module conROM (
  input  [2:0] a,
  input  [1:0] b,
  output [2:0] out_3
);

  ROM #(.addrWidth(5), .dataWidth(3)) rom_1 (.addr({a, b}), .data(out_3));

  // Notes on the sheet:
  //   contents of rom_1 (hex, n*v repeats v):
  //   4*0 1 2 0 0 2 4 0 1 3 6 0 1 4 0 1 2 5 4 1 2 6 4 1 3 7 6 1 3
endmodule
