// Logisim project ejercicio8.circ as structural Verilog: 2 circuits, main circuit main
module main (
  input  [2:0] a,
  output [2:0] x
);

  wire and_1_out, and_2_out, and_3_out, and_4_out, and_5_out, and_6_out, and_7_out, and_8_out, not_1_out,
       not_2_out, not_3_out, or_1_out, or_2_out;

  not not_1 (not_1_out, a[2]);
  not not_2 (not_2_out, a[1]);
  not not_3 (not_3_out, a[0]);
  and and_1 (and_1_out, a[2], not_2_out);
  and and_2 (and_2_out, not_1_out, not_2_out);
  and and_3 (and_3_out, not_1_out, a[1]);
  and and_4 (and_4_out, and_1_out, not_3_out);
  and and_5 (and_5_out, and_2_out, a[0]);
  and and_6 (and_6_out, a[1], not_3_out);
  or or_1 (or_1_out, and_3_out, and_4_out);
  and and_7 (and_7_out, a[1], a[0]);
  or or_2 (or_2_out, and_5_out, and_6_out);
  and and_8 (and_8_out, a[2], a[1]);
  or or_3 (x[1], or_1_out, and_7_out);
  or or_4 (x[0], or_2_out, and_8_out);

  assign x[2] = a[2];
endmodule

module decodificarOR (
  input  [2:0] in_1,
  output [2:0] out_2
);

  wire decoder_1_out0, decoder_1_out1, decoder_1_out2, decoder_1_out3, decoder_1_out4, decoder_1_out5,
       decoder_1_out6, decoder_1_out7;

  Decoder #(.select(3)) decoder_1 (
    .out0(decoder_1_out0), .out1(decoder_1_out1), .out2(decoder_1_out2), .out3(decoder_1_out3),
    .out4(decoder_1_out4), .out5(decoder_1_out5), .out6(decoder_1_out6), .out7(decoder_1_out7), .sel(in_1),
    .en(1'b1));
  or or_1 (out_2[2], decoder_1_out7, decoder_1_out6, decoder_1_out5, decoder_1_out4);
  or or_2 (out_2[1], decoder_1_out7, decoder_1_out4, decoder_1_out3, decoder_1_out2);
  or or_3 (out_2[0], decoder_1_out7, decoder_1_out6, decoder_1_out2, decoder_1_out1);
endmodule
