// Logisim project ejercicio9.circ as structural Verilog: 1 circuit, main circuit main
module main (
  input  [7:0] X,
  input  [7:0] Y,
  output [7:0] out_3
);

  wire adder_1_cout, adder_2_cout, adder_3_cout;
  wire [3:0] adder_2_out, adder_3_out;

  Adder #(.width(4)) adder_1 (.a(X[3:0]), .b(Y[3:0]), .out(out_3[3:0]), .cin(1'b0), .cout(adder_1_cout));
  Adder #(.width(4)) adder_2 (.a(X[7:4]), .b(Y[7:4]), .out(adder_2_out), .cin(1'b0), .cout(adder_2_cout));
  // NoConnect on adder_2_cout
  Adder #(.width(4)) adder_3 (.a(X[7:4]), .b(Y[7:4]), .out(adder_3_out), .cin(1'b1), .cout(adder_3_cout));
  // NoConnect on adder_3_cout
  Multiplexer #(.width(4)) multiplexer_1 (.in0(adder_2_out), .in1(adder_3_out), .out(out_3[7:4]), .sel(adder_1_cout));

  // Notes on the sheet:
  //   t(XOR) = 50ut
  //   t(AND) = t(OR) = t(NOT) = 20ut
  //   Tp: 280ut comparado con 380ut de un Ripple-Carry Adder
endmodule
