// Logisim project ejercicio22.circ as structural Verilog: 6 circuits, main circuit main
module main (
  input  [3:0] in_1
);
endmodule

module HA (
  input  Cin,
  input  X,
  input  Y,
  output S,
  output Cout
);

  wire and_1_out, and_2_out, xor_1_out;

  xor xor_1 (xor_1_out, X, Y);
  and and_1 (and_1_out, X, Y);
  xor xor_2 (S, xor_1_out, Cin);
  and and_2 (and_2_out, xor_1_out, Cin);
  or or_1 (Cout, and_1_out, and_2_out);
endmodule

module FA4bits (
  input  Cin,
  input  [3:0] X,
  input  [3:0] Y,
  output [3:0] S,
  output OvCa2,
  output OvB
);

  wire ha_1_cout, ha_2_cout, ha_3_cout;

  HA ha_1 (.Cin(Cin), .X(X[0]), .Y(Y[0]), .S(S[0]), .Cout(ha_1_cout));
  HA ha_2 (.Cin(ha_1_cout), .X(X[1]), .Y(Y[1]), .S(S[1]), .Cout(ha_2_cout));
  HA ha_3 (.Cin(ha_2_cout), .X(X[2]), .Y(Y[2]), .S(S[2]), .Cout(ha_3_cout));
  HA ha_4 (.Cin(ha_3_cout), .X(X[3]), .Y(Y[3]), .S(S[3]), .Cout(OvB));
  xor xor_1 (OvCa2, ha_3_cout, OvB);
endmodule

module Inversor (
  input  [3:0] X,
  output [3:0] NOT_X
);

  wire fa4bits_1_ovb, fa4bits_1_ovca2;
  wire [3:0] not_1_out;

  assign not_1_out = ~X;  // NOT_Gate not_1, 4 bits wide
  FA4bits fa4bits_1 (.Cin(1'b0), .X(not_1_out), .Y(4'b0001), .S(NOT_X), .OvCa2(fa4bits_1_ovca2), .OvB(fa4bits_1_ovb));
  // NoConnect on fa4bits_1_ovca2
  // NoConnect on fa4bits_1_ovb
endmodule

module ABS_4bits (
  input  [3:0] X,
  output [3:0] ABS_X
);

  wire [3:0] inversor_1_not_x;

  Inversor inversor_1 (.X(X), .NOT_X(inversor_1_not_x));
  Multiplexer #(.width(4)) multiplexer_1 (.in0(X), .in1(inversor_1_not_x), .out(ABS_X), .sel(X[3]));
endmodule

module ABS_FU (
  input  [3:0] X,
  input  [3:0] Y,
  input  SEL,
  output [3:0] W,
  output Ov
);

  wire fa4bits_1_ovb, fa4bits_1_ovca2, fa4bits_2_ovb, fa4bits_2_ovca2;
  wire [3:0] fa4bits_1_s, fa4bits_2_s, inversor_1_not_x, multiplexer_1_out;

  FA4bits fa4bits_1 (.Cin(1'b0), .X(X), .Y(Y), .S(fa4bits_1_s), .OvCa2(fa4bits_1_ovca2), .OvB(fa4bits_1_ovb));
  // NoConnect on fa4bits_1_ovb
  Inversor inversor_1 (.X(Y), .NOT_X(inversor_1_not_x));
  FA4bits fa4bits_2 (
    .Cin(1'b0), .X(X), .Y(inversor_1_not_x), .S(fa4bits_2_s), .OvCa2(fa4bits_2_ovca2), .OvB(fa4bits_2_ovb));
  // NoConnect on fa4bits_2_ovb
  Multiplexer #(.width(4)) multiplexer_1 (.in0(fa4bits_1_s), .in1(fa4bits_2_s), .out(multiplexer_1_out), .sel(SEL));
  or or_1 (Ov, fa4bits_1_ovca2, fa4bits_2_ovca2);
  ABS_4bits abs_4bits_1 (.X(multiplexer_1_out), .ABS_X(W));
endmodule
