// Logisim project Ejercicio15.circ as structural Verilog
module CLCSalida (
  input  A,
  input  B,
  input  CLK,
  input  reset,
  output C
);

  wire decoder_1_out0, decoder_1_out1, decoder_1_out2, decoder_1_out3, decoder_1_out4, decoder_1_out5,
       decoder_1_out6, decoder_1_out7, decoder_1_out8, decoder_1_out9, decoder_1_out10, decoder_1_out11,
       decoder_1_out12, decoder_1_out13, decoder_1_out14, decoder_1_out15, decoder_2_out0, decoder_2_out1,
       decoder_2_out2, decoder_2_out3, or_1_out, or_2_out;
  wire [3:2] d_ff_2_q;

  Decoder #(.select(4)) decoder_1 (
    .out0(decoder_1_out0), .out1(decoder_1_out1), .out2(decoder_1_out2), .out3(decoder_1_out3),
    .out4(decoder_1_out4), .out5(decoder_1_out5), .out6(decoder_1_out6), .out7(decoder_1_out7),
    .out8(decoder_1_out8), .out9(decoder_1_out9), .out10(decoder_1_out10), .out11(decoder_1_out11),
    .out12(decoder_1_out12), .out13(decoder_1_out13), .out14(decoder_1_out14), .out15(decoder_1_out15),
    .sel({d_ff_2_q, B, A}), .en(1'b1));
  or or_1 (or_1_out, decoder_1_out5, decoder_1_out6, decoder_1_out7, decoder_1_out9, decoder_1_out10, decoder_1_out11);
  or or_2 (or_2_out, decoder_1_out3, decoder_1_out4, decoder_1_out8, decoder_1_out9, decoder_1_out10, decoder_1_out11);
  D_Flip_Flop d_ff_1 (.D(or_1_out), .clk(CLK), .Q(d_ff_2_q[3]), .reset(reset));  // open: Qn, preset
  D_Flip_Flop d_ff_2 (.D(or_2_out), .clk(CLK), .Q(d_ff_2_q[2]), .reset(reset));  // open: Qn, preset
  Decoder #(.select(2)) decoder_2 (
    .out0(decoder_2_out0), .out1(decoder_2_out1), .out2(decoder_2_out2), .out3(decoder_2_out3),
    .sel(d_ff_2_q), .en(1'b1));
  or or_3 (C, decoder_2_out0, decoder_2_out3);
endmodule

module E15Sol (
  input  A,
  input  B,
  input  CLK,
  input  reset,
  output C
);

  wire decoder_1_out0, decoder_1_out1, decoder_1_out2, decoder_1_out3;
  wire [1:0] multiplexer_1_out;
  wire [2:1] d_ff_2_q;
  wire [3:0] rom_1_data;

  ROM #(.addrWidth(3), .dataWidth(4)) rom_1 (.addr({d_ff_2_q, B}), .data(rom_1_data));
  Multiplexer #(.width(2)) multiplexer_1 (
    .in0(rom_1_data[3:2]), .in1(rom_1_data[1:0]), .out(multiplexer_1_out), .sel(A));
  D_Flip_Flop d_ff_1 (.D(multiplexer_1_out[1]), .clk(CLK), .Q(d_ff_2_q[2]), .reset(reset));  // open: Qn, preset
  D_Flip_Flop d_ff_2 (.D(multiplexer_1_out[0]), .clk(CLK), .Q(d_ff_2_q[1]), .reset(reset));  // open: Qn, preset
  Decoder #(.select(2)) decoder_1 (
    .out0(decoder_1_out0), .out1(decoder_1_out1), .out2(decoder_1_out2), .out3(decoder_1_out3),
    .sel(d_ff_2_q), .en(1'b1));
  or or_1 (C, decoder_1_out0, decoder_1_out3);

  // Notes on the sheet:
  //   contents of rom_1 (hex, n*v repeats v):
  //   0 1 6 a b f
endmodule
