// Logisim project Ejercicio16.circ as structural Verilog: 1 circuit, main circuit main
module main (
  input  x,
  input  CLK,
  input  reset,
  output out_4
);

  wire anterior_q, xnor_1_out;
  wire [1:0] d_ff_2_q, multiplexer_1_out;
  wire [3:0] rom_1_data;

  ROM #(.addrWidth(2), .dataWidth(4)) rom_1 (.addr(d_ff_2_q), .data(rom_1_data));
  D_Flip_Flop anterior (.D(x), .clk(CLK), .Q(anterior_q), .reset(reset));  // open: Qn, preset
  Multiplexer #(.width(2)) multiplexer_1 (
    .in0(rom_1_data[3:2]), .in1(rom_1_data[1:0]), .out(multiplexer_1_out), .sel(xnor_1_out));
  xnor xnor_1 (xnor_1_out, x, anterior_q);
  D_Flip_Flop d_ff_1 (.D(multiplexer_1_out[1]), .clk(CLK), .Q(d_ff_2_q[1]), .reset(reset));  // open: Qn, preset
  D_Flip_Flop d_ff_2 (.D(multiplexer_1_out[0]), .clk(CLK), .Q(d_ff_2_q[0]), .reset(reset));  // open: Qn, preset
  Multiplexer multiplexer_2 (.in0(anterior_q), .in1(x), .out(out_4), .sel(d_ff_2_q[0]));

  // Notes on the sheet:
  //   contents of rom_1 (hex, n*v repeats v):
  //   4 2 e 8
endmodule
