// Logisim project Ejercicio17.circ as structural Verilog
module Arbol (
  input  speed,
  input  in_2
);

  wire clock_1_out, clsluces_1_luz;

  Clock clock_1 (.out(clock_1_out));
  CLSLuces clsluces_1 (.speed(speed), .clk(clock_1_out), .reset(in_2), .luz(clsluces_1_luz));
  LED led_1 (.in(clsluces_1_luz));
  LED led_2 (.in(clsluces_1_luz));
  LED led_3 (.in(clsluces_1_luz));
  LED led_4 (.in(clsluces_1_luz));
  LED led_5 (.in(clsluces_1_luz));
  LED led_6 (.in(clsluces_1_luz));
  LED led_7 (.in(clsluces_1_luz));
  LED led_8 (.in(clsluces_1_luz));
  LED led_9 (.in(clsluces_1_luz));
  Silueta silueta_1 ();
  LED led_10 (.in(clsluces_1_luz));
  LED led_11 (.in(clsluces_1_luz));
  LED led_12 (.in(clsluces_1_luz));
  LED led_13 (.in(clsluces_1_luz));
  LED led_14 (.in(clsluces_1_luz));
  LED led_15 (.in(clsluces_1_luz));
endmodule

module CLSLuces (
  input  speed,
  input  clk,
  input  reset,
  output luz
);

  wire decoder_1_out0, decoder_1_out1, decoder_1_out2, decoder_1_out3, decoder_1_out4, decoder_1_out5,
       decoder_1_out6, decoder_1_out7, decoder_1_out8, decoder_1_out9, decoder_1_out10, decoder_1_out11;
  wire [2:1] d_ff_2_q;
  wire [3:0] delay1_1_act;

  ROM #(.addrWidth(3), .dataWidth(2)) rom_1 (.addr({d_ff_2_q, speed}), .data(delay1_1_act[3:2]));
  Delay1 delay1_1 (.CLK(clk), .reset(reset), .act(delay1_1_act[0]));
  Delay2 delay2_1 (.CLK(clk), .reset(reset), .act(delay1_1_act[1]));
  D_Flip_Flop d_ff_1 (.D(delay1_1_act[3]), .clk(clk), .Q(d_ff_2_q[2]));  // open: Qn, preset, reset
  D_Flip_Flop d_ff_2 (.D(delay1_1_act[2]), .clk(clk), .Q(d_ff_2_q[1]));  // open: Qn, preset, reset
  Decoder #(.select(4)) decoder_1 (
    .out0(decoder_1_out0), .out1(decoder_1_out1), .out2(decoder_1_out2), .out3(decoder_1_out3),
    .out4(decoder_1_out4), .out5(decoder_1_out5), .out6(decoder_1_out6), .out7(decoder_1_out7),
    .out8(decoder_1_out8), .out9(decoder_1_out9), .out10(decoder_1_out10), .out11(decoder_1_out11),
    .sel(delay1_1_act), .en(1'b1));  // open: out12, out13, out14, out15
  or or_1 (luz, decoder_1_out0, decoder_1_out1, decoder_1_out2, decoder_1_out3, decoder_1_out4, decoder_1_out7, decoder_1_out9, decoder_1_out11);

  // Notes on the sheet:
  //   contents of rom_1 (hex, n*v repeats v):
  //   0 1 1 2 2
endmodule

module Delay1 (
  input  CLK,
  input  reset,
  output act
);

  wire not_1_out;

  not not_1 (not_1_out, act);
  D_Flip_Flop d_ff_1 (.D(not_1_out), .clk(CLK), .Q(act), .reset(reset));  // open: Qn, preset
endmodule

module Delay2 (
  input  CLK,
  input  reset,
  output act
);

  wire [0:0] d_ff_2_q;
  wire [1:0] rom_1_data;

  ROM #(.addrWidth(2), .dataWidth(2)) rom_1 (.addr({act, d_ff_2_q[0]}), .data(rom_1_data));
  D_Flip_Flop d_ff_1 (.D(rom_1_data[1]), .clk(CLK), .Q(act), .reset(reset));  // open: Qn, preset
  D_Flip_Flop d_ff_2 (.D(rom_1_data[0]), .clk(CLK), .Q(d_ff_2_q[0]), .reset(reset));  // open: Qn, preset

  // Notes on the sheet:
  //   contents of rom_1 (hex, n*v repeats v):
  //   1 2
endmodule
