// Logisim project Ejercicio18.circ as structural Verilog: 2 circuits, main circuit main
module main (
  input  B,
  input  reset,
  input  CLK,
  output W1,
  output W0,
  output valid
);

  wire decoder_1_out0, decoder_1_out1, decoder_1_out2, decoder_1_out3, decoder_1_out4, decoder_1_out5,
       decoder_1_out6, decoder_1_out7;
  wire [2:0] d_ff_3_q, multiplexer_1_out;
  wire [5:0] rom_1_data;

  ROM #(.addrWidth(4), .dataWidth(6)) rom_1 (.addr({d_ff_3_q, B}), .data(rom_1_data));
  Multiplexer #(.width(3)) multiplexer_1 (
    .in0(rom_1_data[5:3]), .in1(rom_1_data[2:0]), .out(multiplexer_1_out), .sel(reset));
  D_Flip_Flop d_ff_1 (.D(multiplexer_1_out[2]), .clk(CLK), .Q(d_ff_3_q[2]), .reset(1'b0));  // open: Qn, preset
  D_Flip_Flop d_ff_2 (.D(multiplexer_1_out[1]), .clk(CLK), .Q(d_ff_3_q[1]), .reset(1'b0));  // open: Qn, preset
  D_Flip_Flop d_ff_3 (.D(multiplexer_1_out[0]), .clk(CLK), .Q(d_ff_3_q[0]), .reset(1'b0));  // open: Qn, preset
  Decoder #(.select(3)) decoder_1 (
    .out0(decoder_1_out0), .out1(decoder_1_out1), .out2(decoder_1_out2), .out3(decoder_1_out3),
    .out4(decoder_1_out4), .out5(decoder_1_out5), .out6(decoder_1_out6), .out7(decoder_1_out7),
    .sel(d_ff_3_q), .en(1'b1));
  or or_1 (W1, decoder_1_out6, decoder_1_out7);
  or or_2 (W0, decoder_1_out4, decoder_1_out7);
  or or_3 (valid, decoder_1_out2, decoder_1_out4, decoder_1_out6, decoder_1_out7);

  // Notes on the sheet:
  //   contents of rom_1 (hex, n*v repeats v):
  //   1 1 10 18 10 10 20 28 20 20 30 38 30 30 38 38
endmodule

module Sol (
  input  B,
  input  reset,
  output W1,
  output W0,
  output valid
);

  wire clock_1_out;

  Clock clock_1 (.out(clock_1_out));
  main main_1 (.B(B), .reset(reset), .CLK(clock_1_out), .W1(W1), .W0(W0), .valid(valid));
endmodule
