// Logisim project Ejercicio19.circ as structural Verilog: 1 circuit, main circuit main
module main (
  input  x,
  input  CLK,
  input  reset,
  output W
);

  wire not_1_out, not_2_out;
  wire [1:0] d_ff_3_q, d_ff_4_q, multiplexer_1_out, multiplexer_2_out;
  wire [3:0] rom_1_data, rom_2_data;

  ROM #(.addrWidth(2), .dataWidth(4)) rom_1 (.addr(d_ff_3_q), .data(rom_1_data));
  ROM #(.addrWidth(2), .dataWidth(4)) rom_2 (.addr(d_ff_4_q), .data(rom_2_data));
  Multiplexer #(.width(2)) multiplexer_1 (
    .in0(rom_1_data[3:2]), .in1(rom_1_data[1:0]), .out(multiplexer_1_out), .sel(x));
  Multiplexer #(.width(2)) multiplexer_2 (
    .in0(rom_2_data[3:2]), .in1(rom_2_data[1:0]), .out(multiplexer_2_out), .sel(x));
  D_Flip_Flop d_ff_1 (.D(multiplexer_1_out[1]), .clk(CLK), .Q(d_ff_3_q[1]), .reset(reset));  // open: Qn, preset
  D_Flip_Flop d_ff_2 (.D(multiplexer_2_out[1]), .clk(CLK), .Q(d_ff_4_q[1]), .reset(reset));  // open: Qn, preset
  D_Flip_Flop d_ff_3 (.D(multiplexer_1_out[0]), .clk(CLK), .Q(d_ff_3_q[0]), .reset(reset));  // open: Qn, preset
  not not_1 (not_1_out, d_ff_4_q[0]);
  D_Flip_Flop d_ff_4 (.D(multiplexer_2_out[0]), .clk(CLK), .Q(d_ff_4_q[0]), .reset(reset));  // open: Qn, preset
  not not_2 (not_2_out, d_ff_3_q[0]);
  and and_1 (W, d_ff_3_q[1], not_2_out, d_ff_4_q[1], not_1_out);

  // Notes on the sheet:
  //   contents of rom_1 (hex, n*v repeats v):
  //   4 9 a
  //   contents of rom_2 (hex, n*v repeats v):
  //   1 6 a
endmodule
