// Logisim project Ejercicio21.circ as structural Verilog: 1 circuit, main circuit main
module main (
  input  Bin,
  input  CLK,
  input  reset,
  output Bout
);

  wire d_ff_1_q, d_ff_2_q, not_1_out, not_2_out;
  wire [2:1] and_2_out, multiplexer_1_out;
  wire [2:2] and_1_out;

  not not_1 (not_1_out, d_ff_1_q);
  not not_2 (not_2_out, d_ff_2_q);
  and and_1 (and_1_out[2], not_1_out, d_ff_2_q);
  xor xor_1 (and_2_out[2], d_ff_1_q, d_ff_2_q);
  and and_2 (and_2_out[1], not_1_out, not_2_out);
  Multiplexer #(.width(3)) multiplexer_1 (
    .in0({and_1_out[2], 1'b0, and_1_out[2]}), .in1({and_2_out, and_1_out[2]}),
    .out({multiplexer_1_out, Bout}), .sel(Bin));
  D_Flip_Flop d_ff_1 (.D(multiplexer_1_out[2]), .clk(CLK), .Q(d_ff_1_q), .reset(reset));  // open: Qn, preset
  D_Flip_Flop d_ff_2 (.D(multiplexer_1_out[1]), .clk(CLK), .Q(d_ff_2_q), .reset(reset));  // open: Qn, preset
endmodule
