// Logisim project Ejercicio22.circ as structural Verilog: 3 circuits, main circuit main
module main (
  input  [7:0] entrada,
  input  SLIn,
  input  clk,
  input  reset,
  output [7:0] salida
);

  wire multiplexer_1_out, multiplexer_2_out, multiplexer_3_out, multiplexer_4_out, multiplexer_5_out,
       multiplexer_6_out, multiplexer_7_out, multiplexer_8_out;

  Multiplexer multiplexer_1 (.in0(entrada[7]), .in1(1'b0), .out(multiplexer_1_out), .sel(SLIn));
  D_Flip_Flop d_ff_1 (.D(multiplexer_1_out), .clk(clk), .Q(salida[7]), .reset(reset));  // open: Qn, preset
  Multiplexer multiplexer_2 (.in0(entrada[6]), .in1(salida[7]), .out(multiplexer_2_out), .sel(SLIn));
  D_Flip_Flop d_ff_2 (.D(multiplexer_2_out), .clk(clk), .Q(salida[6]), .reset(reset));  // open: Qn, preset
  Multiplexer multiplexer_3 (.in0(entrada[5]), .in1(salida[6]), .out(multiplexer_3_out), .sel(SLIn));
  D_Flip_Flop d_ff_3 (.D(multiplexer_3_out), .clk(clk), .Q(salida[5]), .reset(reset));  // open: Qn, preset
  Multiplexer multiplexer_4 (.in0(entrada[4]), .in1(salida[5]), .out(multiplexer_4_out), .sel(SLIn));
  D_Flip_Flop d_ff_4 (.D(multiplexer_4_out), .clk(clk), .Q(salida[4]), .reset(reset));  // open: Qn, preset
  Multiplexer multiplexer_5 (.in0(entrada[3]), .in1(salida[4]), .out(multiplexer_5_out), .sel(SLIn));
  D_Flip_Flop d_ff_5 (.D(multiplexer_5_out), .clk(clk), .Q(salida[3]), .reset(reset));  // open: Qn, preset
  Multiplexer multiplexer_6 (.in0(entrada[2]), .in1(salida[3]), .out(multiplexer_6_out), .sel(SLIn));
  D_Flip_Flop d_ff_6 (.D(multiplexer_6_out), .clk(clk), .Q(salida[2]), .reset(reset));  // open: Qn, preset
  Multiplexer multiplexer_7 (.in0(entrada[1]), .in1(salida[2]), .out(multiplexer_7_out), .sel(SLIn));
  D_Flip_Flop d_ff_7 (.D(multiplexer_7_out), .clk(clk), .Q(salida[1]), .reset(reset));  // open: Qn, preset
  Multiplexer multiplexer_8 (.in0(entrada[0]), .in1(salida[1]), .out(multiplexer_8_out), .sel(SLIn));
  D_Flip_Flop d_ff_8 (.D(multiplexer_8_out), .clk(clk), .Q(salida[0]), .reset(reset));  // open: Qn, preset
endmodule

module CuentaCiclos (
  input  CLK,
  input  reset,
  output W
);

  wire [2:0] d_ff_3_q, rom_1_data;

  ROM #(.addrWidth(3), .dataWidth(3)) rom_1 (.addr(d_ff_3_q), .data(rom_1_data));
  D_Flip_Flop d_ff_1 (.D(rom_1_data[2]), .clk(CLK), .Q(d_ff_3_q[2]), .reset(reset));  // open: Qn, preset
  D_Flip_Flop d_ff_2 (.D(rom_1_data[1]), .clk(CLK), .Q(d_ff_3_q[1]), .reset(reset));  // open: Qn, preset
  D_Flip_Flop d_ff_3 (.D(rom_1_data[0]), .clk(CLK), .Q(d_ff_3_q[0]), .reset(reset));  // open: Qn, preset
  ROM #(.addrWidth(3), .dataWidth(1)) rom_2 (.addr(d_ff_3_q));  // open: data

  // Notes on the sheet:
  //   contents of rom_1 (hex, n*v repeats v):
  //   1 2 3 4 5 6 7
  //   contents of rom_2 (hex, n*v repeats v):
  //   0 7*1
endmodule

module ParaleloSerie (
  input  [7:0] B,
  input  reset,
  input  CLK,
  output W
);

  wire cuentaciclos_1_w;
  wire [7:1] main_1_salida;

  CuentaCiclos cuentaciclos_1 (.CLK(CLK), .reset(reset), .W(cuentaciclos_1_w));
  main main_1 (.entrada(B), .SLIn(cuentaciclos_1_w), .clk(CLK), .reset(reset), .salida({main_1_salida, W}));
endmodule
