// Logisim project Ejercicio23.circ as structural Verilog: 1 circuit, main circuit main
module main (
  input  A,
  input  CLK,
  input  reset,
  output W
);

  wire and_1_out, and_2_out, decoder_1_out0, decoder_1_out1, decoder_1_out2, decoder_1_out3, decoder_1_out5,
       decoder_1_out6, decoder_1_out7, not_1_out, not_2_out;
  wire [2:0] d_ff_3_q, multiplexer_1_out, or_4_out;
  wire [2:1] or_3_out;

  Decoder #(.select(3)) decoder_1 (
    .out0(decoder_1_out0), .out1(decoder_1_out1), .out2(decoder_1_out2), .out3(decoder_1_out3),
    .out4(or_4_out[2]), .out5(decoder_1_out5), .out6(decoder_1_out6), .out7(decoder_1_out7), .sel(d_ff_3_q));  // open: en
  or or_1 (or_4_out[1], decoder_1_out6, decoder_1_out2);
  or or_2 (or_3_out[2], decoder_1_out0, decoder_1_out2, decoder_1_out3, or_4_out[2], decoder_1_out5, decoder_1_out6);
  or or_3 (or_3_out[1], decoder_1_out1, decoder_1_out3, decoder_1_out5);
  or or_4 (or_4_out[0], decoder_1_out0, decoder_1_out1, decoder_1_out2, decoder_1_out3, or_4_out[2], decoder_1_out5, decoder_1_out6);
  Multiplexer #(.width(3)) multiplexer_1 (.in0({or_3_out, 1'b0}), .in1(or_4_out), .out(multiplexer_1_out), .sel(A));
  D_Flip_Flop d_ff_1 (.D(multiplexer_1_out[2]), .clk(CLK), .Q(d_ff_3_q[2]), .reset(reset));  // open: Qn, preset
  D_Flip_Flop d_ff_2 (.D(multiplexer_1_out[1]), .clk(CLK), .Q(d_ff_3_q[1]), .reset(reset));  // open: Qn, preset
  D_Flip_Flop d_ff_3 (.D(multiplexer_1_out[0]), .clk(CLK), .Q(d_ff_3_q[0]), .reset(reset));  // open: Qn, preset
  not not_1 (not_1_out, d_ff_3_q[2]);
  and and_1 (and_1_out, not_1_out, d_ff_3_q[1], d_ff_3_q[0]);
  and and_2 (and_2_out, d_ff_3_q[2], d_ff_3_q[1], not_2_out);
  not not_2 (not_2_out, d_ff_3_q[0]);
  or or_5 (W, and_1_out, and_2_out);
endmodule
