// Logisim project Ejercicio24.circ as structural Verilog: 3 circuits, main circuit main
module main (
  input  x,
  input  y,
  input  carry_on,
  input  CLK,
  output w
);

  wire and_1_out, and_2_out, and_3_out, carry_q, or_1_out, xor_1_out;

  xor xor_1 (xor_1_out, x, y);
  and and_1 (and_1_out, x, y);
  xor xor_2 (w, carry_q, xor_1_out);
  and and_2 (and_2_out, carry_q, xor_1_out);
  or or_1 (or_1_out, and_2_out, and_1_out);
  and and_3 (and_3_out, or_1_out, carry_on);
  D_Flip_Flop carry (.D(and_3_out), .clk(CLK), .Q(carry_q));  // open: Qn, preset, reset
endmodule

module contador (
  input  reset,
  input  CLK,
  output W
);

  wire and_1_out, and_2_out, d_ff_1_q, d_ff_2_q, not_2_out;
  wire [1:0] multiplexer_1_out, not_1_out;

  not not_1 (not_1_out[0], d_ff_2_q);
  not not_2 (not_2_out, d_ff_1_q);
  and and_1 (and_1_out, d_ff_2_q, not_2_out);
  and and_2 (and_2_out, d_ff_1_q, not_1_out[0]);
  or or_1 (not_1_out[1], and_1_out, and_2_out);
  Multiplexer #(.width(2)) multiplexer_1 (.in0(not_1_out), .in1(2'b00), .out(multiplexer_1_out), .sel(reset));
  D_Flip_Flop d_ff_1 (.D(multiplexer_1_out[1]), .clk(CLK), .Q(d_ff_1_q));  // open: Qn, preset, reset
  D_Flip_Flop d_ff_2 (.D(multiplexer_1_out[0]), .clk(CLK), .Q(d_ff_2_q));  // open: Qn, preset, reset
  or or_2 (W, d_ff_1_q, d_ff_2_q);
endmodule

module sumador (
  input  x,
  input  y,
  input  CLK,
  input  reset,
  output S
);

  wire contador_1_w;

  contador contador_1 (.reset(reset), .CLK(CLK), .W(contador_1_w));
  main main_1 (.x(x), .y(y), .carry_on(contador_1_w), .CLK(CLK), .w(S));
endmodule
