// Logisim project Ejercicio9.circ as structural Verilog: 1 circuit, main circuit main
module main (
  input  in0,
  input  in1,
  output out0
);

  wire clk_out;
  wire [1:0] d_ff_1_q, multiplexer_1_out;
  wire [8:1] ROM_out;

  Clock clk (.out(clk_out));
  D_Flip_Flop d_ff_1 (.D(multiplexer_1_out[0]), .clk(clk_out), .Q(d_ff_1_q[0]));  // open: Qn, preset, reset
  D_Flip_Flop d_ff_2 (.D(multiplexer_1_out[1]), .clk(clk_out), .Q(d_ff_1_q[1]));  // open: Qn, preset, reset
  PLA #(.out_width(9), .\table ("00 000100100\n01 001100100\n10 000100110\n11 000100101")) ROM (
    .in(d_ff_1_q), .out({ROM_out, out0}));
  Multiplexer #(.select(2), .width(2)) multiplexer_1 (
    .in0(ROM_out[2:1]), .in1(ROM_out[4:3]), .in2(ROM_out[6:5]), .in3(ROM_out[8:7]), .out(multiplexer_1_out),
    .sel({in1, in0}));

  // Notes on the sheet:
  //   tpd: 260ut
endmodule
