// Logisim project ejercicio1.circ as structural Verilog: 1 circuit, main circuit main
module main (
  input  e1,
  input  e2,
  input  RESET,
  input  CLK
);

  wire decoder_1_out0, decoder_1_out1, decoder_1_out2, decoder_1_out3, or_1_out;
  wire [1:0] rom_1_data;
  wire [3:2] FF0_q;

  ROM #(.addrWidth(4), .dataWidth(2)) rom_1 (.addr({FF0_q, e1, e2}), .data(rom_1_data));
  D_Flip_Flop FF1 (.D(rom_1_data[1]), .clk(CLK), .Q(FF0_q[3]), .reset(RESET));  // open: Qn, preset
  D_Flip_Flop FF0 (.D(rom_1_data[0]), .clk(CLK), .Q(FF0_q[2]), .reset(RESET));  // open: Qn, preset
  Decoder #(.select(2)) decoder_1 (
    .out0(decoder_1_out0), .out1(decoder_1_out1), .out2(decoder_1_out2), .out3(decoder_1_out3), .sel(FF0_q),
    .en(1'b1));
  or or_1 (or_1_out, FF0_q[3], decoder_1_out1);
  LED L_1 (.in(decoder_1_out3));
  LED L_0 (.in(or_1_out));

  // Notes on the sheet:
  //   contents of rom_1 (hex, n*v repeats v):
  //   0 1 0 0 1 0 2 1 2 3 1 2 3 2 3 3
endmodule
