// Logisim project ejercicio10.circ as structural Verilog: 1 circuit, main circuit main
module main (
  input  SDcho,
  input  SIzqd,
  input  CLK,
  input  RESET,
  output giro,
  output direccion
);

  wire d_ff_1_q, FF1_q, not_1_out, not_2_out;

  not not_1 (not_1_out, SIzqd);
  not not_2 (not_2_out, SDcho);
  D_Flip_Flop FF1 (.D(SDcho), .clk(CLK), .Q(FF1_q), .reset(RESET));  // open: Qn, preset
  D_Flip_Flop d_ff_1 (.D(SIzqd), .clk(CLK), .Q(d_ff_1_q), .reset(RESET));  // open: Qn, preset
  xor xor_1 (giro, FF1_q, d_ff_1_q);
  not not_3 (direccion, d_ff_1_q);
endmodule
