// Logisim project ejercicio12.circ as structural Verilog: 1 circuit, main circuit main
module main (
  input  entrada,
  input  CLK,
  input  RESET,
  output salida
);

  wire FF0_q, FF1_q, not_1_out, or_1_out, or_2_out;

  not not_1 (not_1_out, FF1_q);
  or or_1 (or_1_out, not_1_out, FF0_q);
  D_Flip_Flop FF1 (.D(or_2_out), .clk(CLK), .Q(FF1_q), .reset(RESET));  // open: Qn, preset
  or or_2 (or_2_out, FF1_q, entrada);
  D_Flip_Flop FF0 (.D(or_1_out), .clk(CLK), .Q(FF0_q), .reset(RESET));  // open: Qn, preset
  and and_1 (salida, FF1_q, FF0_q);
endmodule
