// Logisim project ejercicio13.circ as structural Verilog: 1 circuit, main circuit main
module main (
  input  in_1
);

  wire and_1_out, not_1_out, not_2_out, not_3_out, not_4_out, or_1_out;
  wire [2:0] adder_1_out, d_ff_3_q, multiplexer_1_out;

  not not_1 (not_1_out, in_1);
  not not_2 (not_2_out, d_ff_3_q[2]);
  not not_3 (not_3_out, d_ff_3_q[1]);
  not not_4 (not_4_out, d_ff_3_q[0]);
  and and_1 (and_1_out, in_1, not_2_out, not_3_out, not_4_out);
  // AND_Gate and_2 is placed but not wired
  Adder #(.width(3)) adder_1 (.a(d_ff_3_q), .b(3'b001), .out(adder_1_out));  // open: cin, cout
  buf or_1 (or_1_out, and_1_out);  // OR_Gate
  Multiplexer #(.width(3)) multiplexer_1 (.in0(d_ff_3_q), .in1(adder_1_out), .out(multiplexer_1_out), .sel(or_1_out));
  D_Flip_Flop d_ff_1 (.Q(d_ff_3_q[2]));  // open: D, clk, Qn, preset, reset
  D_Flip_Flop d_ff_2 (.Q(d_ff_3_q[1]));  // open: D, clk, Qn, preset, reset
  D_Flip_Flop d_ff_3 (.Q(d_ff_3_q[0]));  // open: D, clk, Qn, preset, reset
endmodule
