// Logisim project ejercicio4.circ as structural Verilog: 1 circuit, main circuit main
module main (
  input  Em,
  input  Dcha,
  input  Izqd,
  input  OFF,
  output D,
  output I
);

  ROM #(.addrWidth(4), .dataWidth(2)) rom_1 (.addr({Em, Dcha, Izqd, OFF}), .data({I, D}));

  // Notes on the sheet:
  //   contents of rom_1 (hex, n*v repeats v):
  //   0 0 2 0 1 1 1 9*3
endmodule
