// Logisim project ejercicio5.circ as structural Verilog: 1 circuit, main circuit main
module main (
  input  C,
  input  E,
  input  CLK,
  input  RESET,
  output VALID
);

  wire [1:0] rom_1_data;
  wire [3:2] FF0_q;

  ROM #(.addrWidth(4), .dataWidth(2)) rom_1 (.addr({FF0_q, C, E}), .data(rom_1_data));
  D_Flip_Flop FF1 (.D(rom_1_data[1]), .clk(CLK), .Q(FF0_q[3]), .reset(RESET));  // open: Qn, preset
  D_Flip_Flop FF0 (.D(rom_1_data[0]), .clk(CLK), .Q(FF0_q[2]), .reset(RESET));  // open: Qn, preset
  and and_1 (VALID, FF0_q[3], FF0_q[2]);

  // Notes on the sheet:
  //   contents of rom_1 (hex, n*v repeats v):
  //   0 0 1 2 1 1 2 3 2 2 3 3
endmodule
