// Logisim project ejercicio6.circ as structural Verilog: 1 circuit, main circuit main
module main (
  input  A,
  input  RESET,
  output X,
  output W
);

  wire and_2_out, clock_1_out, decoder_1_out1, decoder_1_out3, not_1_out, not_2_out;
  wire [2:1] FF0_q;

  Decoder #(.select(3)) decoder_1 (
    .out1(decoder_1_out1), .out3(decoder_1_out3), .sel({FF0_q, A}), .en(1'b1));  // open: out0, out2, out4, out5, out6, out7
  Clock clock_1 (.out(clock_1_out));
  D_Flip_Flop FF1 (.D(decoder_1_out3), .clk(clock_1_out), .Q(FF0_q[2]), .reset(RESET));  // open: Qn, preset
  D_Flip_Flop FF0 (.D(decoder_1_out1), .clk(clock_1_out), .Q(FF0_q[1]), .reset(RESET));  // open: Qn, preset
  not not_1 (not_1_out, FF0_q[2]);
  not not_2 (not_2_out, FF0_q[1]);
  and and_1 (W, FF0_q[2], not_2_out);
  and and_2 (and_2_out, not_1_out, FF0_q[1]);
  or or_1 (X, W, and_2_out);
endmodule
