// Logisim project ejercicio8.circ as structural Verilog: 2 circuits, main circuit main
module main (
  input  Bit,
  input  CLK,
  input  RESET,
  input  Activacion,
  output W
);

  wire encriptado_1_w;

  encriptado encriptado_1 (.Activacion(Activacion), .Bit(Bit), .CLK(CLK), .RESET(RESET), .W(encriptado_1_w));
  Multiplexer multiplexer_1 (.in0(Bit), .in1(encriptado_1_w), .out(W), .sel(Activacion));
endmodule

module encriptado (
  input  Activacion,
  input  Bit,
  input  CLK,
  input  RESET,
  output W
);

  wire not_1_out, or_1_out;
  wire [0:0] d_ff_1_q;

  ROM #(.addrWidth(2), .dataWidth(1)) rom_1 (.addr({Activacion, d_ff_1_q[0]}));  // open: data
  D_Flip_Flop d_ff_1 (.clk(CLK), .Q(d_ff_1_q[0]));  // open: D, Qn, preset, reset
  or or_1 (or_1_out, RESET, not_1_out);
  not not_1 (not_1_out, Activacion);
  xnor xnor_1 (W, Bit, d_ff_1_q[0]);

  // Notes on the sheet:
  //   contents of rom_1 (hex, n*v repeats v):
  //   0 0 1
endmodule
