// Logisim project ejercicio9.circ as structural Verilog: 1 circuit, main circuit main
module main (
  input  X,
  input  Activacion,
  output out_3
);

  wire clock_1_out, d_ff_1_q, not_1_out, not_2_out, not_3_out, or_1_out;

  Clock clock_1 (.out(clock_1_out));
  D_Flip_Flop d_ff_1 (.D(not_1_out), .clk(clock_1_out), .Q(d_ff_1_q));  // open: Qn, preset, reset
  not not_1 (not_1_out, d_ff_1_q);
  not not_2 (not_2_out, X);
  Multiplexer multiplexer_1 (.in0(not_2_out), .in1(X), .out(out_3), .sel(or_1_out));
  or or_1 (or_1_out, d_ff_1_q, not_3_out);
  not not_3 (not_3_out, Activacion);
endmodule
