// Logisim project ejercicio_7.circ as structural Verilog: 3 circuits, main circuit main
module main (
  input  P,
  input  CLK,
  input  RESET,
  output Delay
);

  wire [1:0] rom_1_data;
  wire [2:1] FF0_q;

  ROM #(.addrWidth(3), .dataWidth(2)) rom_1 (.addr({FF0_q, P}), .data(rom_1_data));
  D_Flip_Flop FF1 (.D(rom_1_data[1]), .clk(CLK), .Q(FF0_q[2]), .reset(RESET));  // open: Qn, preset
  D_Flip_Flop FF0 (.D(rom_1_data[0]), .clk(CLK), .Q(FF0_q[1]), .reset(RESET));  // open: Qn, preset
  and and_1 (Delay, FF0_q[2], FF0_q[1]);

  // Notes on the sheet:
  //   contents of rom_1 (hex, n*v repeats v):
  //   0 1 2 2 3 3 0 3
endmodule

module cycle_counter_six (
  input  in_1,
  input  CLK,
  input  RESET,
  output delay
);

  wire main_1_delay;

  main main_1 (.P(in_1), .CLK(CLK), .RESET(RESET), .Delay(main_1_delay));
  main main_2 (.P(main_1_delay), .CLK(CLK), .RESET(RESET), .Delay(delay));
endmodule

module semaforo (
  input  P,
  input  RESET,
  input  CLK
);

  wire and_1_out, and_2_out, and_3_out, and_4_out, and_5_out, and_6_out, cycle_counter_six_1_delay, D1_out,
       D2_out, FF0_q, FF1_q, main_1_delay, not_1_out, not_2_out, not_3_out, not_4_out, or_1_out, or_2_out;

  main main_1 (.P(P), .CLK(CLK), .RESET(RESET), .Delay(main_1_delay));
  cycle_counter_six cycle_counter_six_1 (.in_1(P), .CLK(CLK), .RESET(RESET), .delay(cycle_counter_six_1_delay));
  and and_1 (and_1_out, not_1_out, FF0_q, main_1_delay);
  and and_2 (and_2_out, D2_out, FF1_q, not_2_out);
  and and_3 (and_3_out, not_1_out, not_2_out, P);
  and and_4 (and_4_out, not_1_out, FF0_q, D1_out);
  not D1 (D1_out, main_1_delay);
  not D2 (D2_out, cycle_counter_six_1_delay);
  or or_1 (or_1_out, and_1_out, and_2_out);
  not not_1 (not_1_out, FF1_q);
  or or_2 (or_2_out, and_3_out, and_4_out);
  not not_2 (not_2_out, FF0_q);
  and and_5 (and_5_out, not_3_out, FF0_q);
  D_Flip_Flop FF1 (.D(or_1_out), .clk(CLK), .Q(FF1_q), .reset(RESET));  // open: Qn, preset
  D_Flip_Flop FF0 (.D(or_2_out), .clk(CLK), .Q(FF0_q), .reset(RESET));  // open: Qn, preset
  LED led_1 (.in(and_6_out));
  LED led_2 (.in(and_5_out));
  LED led_3 (.in(not_3_out));
  not not_3 (not_3_out, FF1_q);
  not not_4 (not_4_out, FF0_q);
  and and_6 (and_6_out, FF1_q, not_4_out);
endmodule
