// Logisim project Ejercicio20.circ as structural Verilog: 2 circuits, main circuit CLC
module CLC (
  input  q1,
  input  q0,
  input  i3,
  input  i2,
  input  i1,
  input  i0,
  output o1,
  output q1mas,
  output q0mas
);

  wire and_2_out, and_3_out, and_4_out, and_5_out, and_6_out, and_7_out, and_8_out, and_9_out, and_10_out,
       and_11_out, and_12_out, and_13_out, and_14_out, and_15_out, and_16_out, and_17_out, and_18_out,
       and_19_out, and_20_out, and_21_out, and_22_out, and_23_out, not_1_out, not_2_out, not_3_out,
       not_4_out, not_5_out, not_6_out, or_1_out, or_3_out, or_5_out;

  not not_1 (not_1_out, q1);
  not not_2 (not_2_out, q0);
  not not_3 (not_3_out, i3);
  not not_4 (not_4_out, i2);
  not not_5 (not_5_out, i1);
  and and_1 (o1, q1, q0);
  and and_2 (and_2_out, q1, not_2_out);
  or or_1 (or_1_out, o1, and_2_out);
  and and_3 (and_3_out, not_1_out, q0);
  or or_2 (q1mas, or_1_out, and_7_out);
  and and_4 (and_4_out, i3, i2);
  and and_5 (and_5_out, i1, i0);
  and and_6 (and_6_out, and_4_out, and_5_out);
  and and_7 (and_7_out, and_3_out, and_6_out);
  and and_8 (and_8_out, q1, q0);
  and and_9 (and_9_out, q1, not_2_out);
  and and_10 (and_10_out, and_9_out, and_13_out);
  or or_3 (or_3_out, and_8_out, and_10_out);
  and and_11 (and_11_out, not_3_out, i2);
  and and_12 (and_12_out, not_5_out, i0);
  and and_13 (and_13_out, and_11_out, and_12_out);
  and and_14 (and_14_out, not_1_out, q0);
  or or_4 (q0mas, or_3_out, or_5_out);
  and and_15 (and_15_out, i3, i2);
  and and_16 (and_16_out, i1, i0);
  and and_17 (and_17_out, and_15_out, and_16_out);
  not not_6 (not_6_out, and_17_out);
  and and_18 (and_18_out, and_14_out, not_6_out);
  and and_19 (and_19_out, not_1_out, not_2_out);
  or or_5 (or_5_out, and_18_out, and_23_out);
  and and_20 (and_20_out, i1, i0);
  and and_21 (and_21_out, not_3_out, not_4_out);
  and and_22 (and_22_out, and_21_out, and_20_out);
  and and_23 (and_23_out, and_19_out, and_22_out);
endmodule

module CajaFuerte (
  input  [3:0] in_1,
  output out_2
);

  wire clc_1_q0mas, clc_1_q1mas, clock_1_out, d_ff_1_q, d_ff_2_q;

  Clock clock_1 (.out(clock_1_out));
  D_Flip_Flop d_ff_1 (.D(clc_1_q0mas), .clk(clock_1_out), .Q(d_ff_1_q));  // open: Qn, preset, reset
  D_Flip_Flop d_ff_2 (.D(clc_1_q1mas), .clk(clock_1_out), .Q(d_ff_2_q));  // open: Qn, preset, reset
  CLC clc_1 (
    .q0(d_ff_1_q), .i3(in_1[3]), .i2(in_1[2]), .i1(in_1[1]), .i0(in_1[0]), .q1(d_ff_2_q), .o1(out_2),
    .q1mas(clc_1_q1mas), .q0mas(clc_1_q0mas));

  // Notes on the sheet:
  //   Combinación: 3 - F - 5
  //   RAZÓN: t(IN-BB) > 200ut
  //   No funcionará con esa especificación de reloj.
endmodule
