// Logisim project MCD.circ as structural Verilog
module UP (
  input  [15:0] Y,
  input  [15:0] X,
  input  CLK,
  input  LDA,
  input  LDB,
  input  MX1,
  input  MX2,
  input  RESET,
  output AgtB,
  output AneqB
);

  wire comparator_1_eq;
  wire [15:0] multiplexer_1_out, multiplexer_2_out, register_1_q, register_2_q, subtractor_1_out;

  not not_1 (AneqB, comparator_1_eq);
  Multiplexer #(.width(16)) multiplexer_1 (.in0(X), .in1(subtractor_1_out), .out(multiplexer_1_out), .sel(MX1));
  Register #(.width(16)) register_1 (.D(multiplexer_1_out), .en(LDA), .clk(CLK), .Q(register_1_q), .clr(RESET));
  Comparator #(.width(16)) comparator_1 (
    .a(register_1_q), .b(register_2_q), .gt(AgtB), .eq(comparator_1_eq));  // open: lt
  Register #(.width(16)) register_2 (.D(multiplexer_2_out), .en(LDB), .clk(CLK), .Q(register_2_q), .clr(RESET));
  Multiplexer #(.width(16)) multiplexer_2 (.in0(Y), .in1(subtractor_1_out), .out(multiplexer_2_out), .sel(MX2));
  Subtractor #(.width(16)) subtractor_1 (
    .a(register_1_q), .b(register_2_q), .out(subtractor_1_out));  // open: bin, bout
endmodule

module UC (
  input  INI,
  input  AgtB,
  input  in_3
);
endmodule
