// Logisim project bancoDeRegistros.circ as structural Verilog: 8 circuits, main circuit main
module main (
  input  [2:0] in_1,
  input  [2:0] in_2,
  input  in_3,
  input  in_4,
  input  [15:0] in_5,
  input  [2:0] in_6,
  output [15:0] out_7,
  output [15:0] out_8
);

  wire clock_1_out;

  Clock clock_1 (.out(clock_1_out));
  regFile regfile_1 (
    .CLK(clock_1_out), .AddrA(in_1), .AddrB(in_2), .R(in_3), .RW(in_4), .D(in_5), .AddrD(in_6), .A(out_7),
    .B(out_8));
endmodule

module basic_biestable (
);

  wire not_1_out, not_2_out;

  not not_1 (not_1_out, not_2_out);
  not not_2 (not_2_out, not_1_out);
endmodule

module sr_latch (
  input  R,
  input  S,
  output Q
);

  wire nor_2_out;

  nor nor_1 (Q, R, nor_2_out);
  nor nor_2 (nor_2_out, Q, S);
endmodule

module d_latch (
  input  CLK,
  input  D,
  output Q
);

  wire and_1_out, and_2_out, not_1_out;

  and and_1 (and_1_out, CLK, D);
  not not_1 (not_1_out, D);
  and and_2 (and_2_out, CLK, not_1_out);
  sr_latch sr_latch_1 (.R(and_2_out), .S(and_1_out), .Q(Q));
endmodule

module flip_flop_d (
  input  CLK,
  input  D,
  output Q
);

  wire d_latch_1_q, not_1_out;

  not not_1 (not_1_out, CLK);
  d_latch d_latch_1 (.CLK(CLK), .D(D), .Q(d_latch_1_q));
  d_latch d_latch_2 (.CLK(not_1_out), .D(d_latch_1_q), .Q(Q));

  // Notes on the sheet:
  //   Leader
  //   Slave
endmodule

module r_rw_flip_flop_d (
  input  CLK,
  input  E,
  input  D,
  input  R,
  output Q
);

  wire and_1_out, and_2_out, not_1_out;

  not not_1 (not_1_out, R);
  and and_1 (and_1_out, CLK, E);
  and and_2 (and_2_out, D, not_1_out);
  flip_flop_d flip_flop_d_1 (.CLK(and_1_out), .D(and_2_out), .Q(Q));
endmodule

module P3D6REG16b (
  input  CLK,
  input  E,
  input  R,
  input  [15:0] D,
  output [15:0] Q
);

  r_rw_flip_flop_d r_rw_flip_flop_d_1 (.CLK(CLK), .E(E), .D(D[0]), .R(R), .Q(Q[0]));
  r_rw_flip_flop_d r_rw_flip_flop_d_2 (.CLK(CLK), .E(E), .D(D[1]), .R(R), .Q(Q[1]));
  r_rw_flip_flop_d r_rw_flip_flop_d_3 (.CLK(CLK), .E(E), .D(D[2]), .R(R), .Q(Q[2]));
  r_rw_flip_flop_d r_rw_flip_flop_d_4 (.CLK(CLK), .E(E), .D(D[3]), .R(R), .Q(Q[3]));
  r_rw_flip_flop_d r_rw_flip_flop_d_5 (.CLK(CLK), .E(E), .D(D[4]), .R(R), .Q(Q[4]));
  r_rw_flip_flop_d r_rw_flip_flop_d_6 (.CLK(CLK), .E(E), .D(D[5]), .R(R), .Q(Q[5]));
  r_rw_flip_flop_d r_rw_flip_flop_d_7 (.CLK(CLK), .E(E), .D(D[6]), .R(R), .Q(Q[6]));
  r_rw_flip_flop_d r_rw_flip_flop_d_8 (.CLK(CLK), .E(E), .D(D[7]), .R(R), .Q(Q[7]));
  r_rw_flip_flop_d r_rw_flip_flop_d_9 (.CLK(CLK), .E(E), .D(D[8]), .R(R), .Q(Q[8]));
  r_rw_flip_flop_d r_rw_flip_flop_d_10 (.CLK(CLK), .E(E), .D(D[9]), .R(R), .Q(Q[9]));
  r_rw_flip_flop_d r_rw_flip_flop_d_11 (.CLK(CLK), .E(E), .D(D[10]), .R(R), .Q(Q[10]));
  r_rw_flip_flop_d r_rw_flip_flop_d_12 (.CLK(CLK), .E(E), .D(D[11]), .R(R), .Q(Q[11]));
  r_rw_flip_flop_d r_rw_flip_flop_d_13 (.CLK(CLK), .E(E), .D(D[12]), .R(R), .Q(Q[12]));
  r_rw_flip_flop_d r_rw_flip_flop_d_14 (.CLK(CLK), .E(E), .D(D[13]), .R(R), .Q(Q[13]));
  r_rw_flip_flop_d r_rw_flip_flop_d_15 (.CLK(CLK), .E(E), .D(D[14]), .R(R), .Q(Q[14]));
  r_rw_flip_flop_d r_rw_flip_flop_d_16 (.CLK(CLK), .E(E), .D(D[15]), .R(R), .Q(Q[15]));
endmodule

module regFile (
  input  CLK,
  input  [2:0] AddrA,
  input  [2:0] AddrB,
  input  R,
  input  RW,
  input  [15:0] D,
  input  [2:0] AddrD,
  output [15:0] A,
  output [15:0] B
);

  wire demultiplexer_1_out0, demultiplexer_1_out1, demultiplexer_1_out2, demultiplexer_1_out3,
       demultiplexer_1_out4, demultiplexer_1_out5, demultiplexer_1_out6, demultiplexer_1_out7;
  wire [15:0] demultiplexer_2_out0, demultiplexer_2_out1, demultiplexer_2_out2, demultiplexer_2_out3,
       demultiplexer_2_out4, demultiplexer_2_out5, demultiplexer_2_out6, demultiplexer_2_out7,
       p3d6reg16b_1_q, p3d6reg16b_2_q, p3d6reg16b_3_q, p3d6reg16b_4_q, p3d6reg16b_5_q, p3d6reg16b_6_q,
       p3d6reg16b_7_q, p3d6reg16b_8_q;

  Demultiplexer #(.select(3)) demultiplexer_1 (
    .out0(demultiplexer_1_out0), .out1(demultiplexer_1_out1), .out2(demultiplexer_1_out2),
    .out3(demultiplexer_1_out3), .out4(demultiplexer_1_out4), .out5(demultiplexer_1_out5),
    .out6(demultiplexer_1_out6), .out7(demultiplexer_1_out7), .in(RW), .sel(AddrD));
  Demultiplexer #(.select(3), .width(16)) demultiplexer_2 (
    .out0(demultiplexer_2_out0), .out1(demultiplexer_2_out1), .out2(demultiplexer_2_out2),
    .out3(demultiplexer_2_out3), .out4(demultiplexer_2_out4), .out5(demultiplexer_2_out5),
    .out6(demultiplexer_2_out6), .out7(demultiplexer_2_out7), .in(D), .sel(AddrD));
  P3D6REG16b p3d6reg16b_1 (.CLK(CLK), .E(demultiplexer_1_out0), .R(R), .D(demultiplexer_2_out0), .Q(p3d6reg16b_1_q));
  P3D6REG16b p3d6reg16b_2 (.CLK(CLK), .E(demultiplexer_1_out1), .R(R), .D(demultiplexer_2_out1), .Q(p3d6reg16b_2_q));
  P3D6REG16b p3d6reg16b_3 (.CLK(CLK), .E(demultiplexer_1_out2), .R(R), .D(demultiplexer_2_out2), .Q(p3d6reg16b_3_q));
  P3D6REG16b p3d6reg16b_4 (.CLK(CLK), .E(demultiplexer_1_out3), .R(R), .D(demultiplexer_2_out3), .Q(p3d6reg16b_4_q));
  P3D6REG16b p3d6reg16b_5 (.CLK(CLK), .E(demultiplexer_1_out4), .R(R), .D(demultiplexer_2_out4), .Q(p3d6reg16b_5_q));
  P3D6REG16b p3d6reg16b_6 (.CLK(CLK), .E(demultiplexer_1_out5), .R(R), .D(demultiplexer_2_out5), .Q(p3d6reg16b_6_q));
  P3D6REG16b p3d6reg16b_7 (.CLK(CLK), .E(demultiplexer_1_out6), .R(R), .D(demultiplexer_2_out6), .Q(p3d6reg16b_7_q));
  P3D6REG16b p3d6reg16b_8 (.CLK(CLK), .E(demultiplexer_1_out7), .R(R), .D(demultiplexer_2_out7), .Q(p3d6reg16b_8_q));
  Multiplexer #(.select(3), .width(16)) multiplexer_1 (
    .in0(p3d6reg16b_1_q), .in1(p3d6reg16b_2_q), .in2(p3d6reg16b_3_q), .in3(p3d6reg16b_4_q),
    .in4(p3d6reg16b_5_q), .in5(p3d6reg16b_6_q), .in6(p3d6reg16b_7_q), .in7(p3d6reg16b_8_q), .out(A),
    .sel(AddrA));
  Multiplexer #(.select(3), .width(16)) multiplexer_2 (
    .in0(p3d6reg16b_1_q), .in1(p3d6reg16b_2_q), .in2(p3d6reg16b_3_q), .in3(p3d6reg16b_4_q),
    .in4(p3d6reg16b_5_q), .in5(p3d6reg16b_6_q), .in6(p3d6reg16b_7_q), .in7(p3d6reg16b_8_q), .out(B),
    .sel(AddrB));
endmodule
