// Logisim project cajaFuerte.circ as structural Verilog: 1 circuit, main circuit main
module main (
  input  [1:0] num,
  input  push,
  input  reset,
  output blocked,
  output opened
);

  wire and_1_out, and_2_out, and_3_out, and_4_out, and_5_out, and_6_out, clock_1_out, not_1_out, not_2_out,
       or_1_out, or_2_out;
  wire [0:0] multiplexer_1_out;
  wire [1:0] register_1_q;
  wire [2:0] adder_1_out, multiplexer_2_out;

  not not_1 (not_1_out, num[1]);
  // NoConnect on num[1]
  // NoConnect on not_1_out
  not not_2 (not_2_out, num[0]);
  // NoConnect on num[0]
  // NoConnect on not_2_out
  and and_1 (and_1_out, not_2_out, not_1_out);
  and and_2 (and_2_out, num[0], not_1_out);
  and and_3 (and_3_out, not_2_out, num[1]);
  and and_4 (and_4_out, num[0], num[1]);
  Multiplexer #(.select(2)) multiplexer_1 (
    .in0(and_1_out), .in1(and_4_out), .in2(and_3_out), .in3(and_2_out), .out(multiplexer_1_out[0]),
    .sel(register_1_q));
  Clock clock_1 (.out(clock_1_out));
  Multiplexer #(.width(3)) multiplexer_2 (
    .in0({2'b00, multiplexer_1_out[0]}), .in1(3'b000), .out(multiplexer_2_out), .sel(or_2_out));
  Adder #(.width(3)) adder_1 (
    .a(multiplexer_2_out), .b({blocked, register_1_q}), .out(adder_1_out), .cin(1'b0));  // open: cout
  and and_5 (and_5_out, blocked, and_6_out);
  and and_6 (and_6_out, register_1_q[0], register_1_q[1]);
  Register #(.width(3)) register_1 (
    .D(adder_1_out), .en(push), .clk(clock_1_out), .Q({blocked, register_1_q}), .clr(or_1_out));
  or or_1 (or_1_out, reset, and_5_out);
  or or_2 (or_2_out, blocked, opened);
  and and_7 (opened, register_1_q[0], register_1_q[1]);
endmodule
