// Logisim project PPG.circ as structural Verilog
module COMP (
  input  [15:0] A,
  input  [15:0] B,
  input  [2:0] F,
  output [15:0] out_4
);

  wire comparator_1_eq, comparator_1_lt, comparator_2_eq, comparator_2_lt, or_1_out, or_2_out;
  wire [15:0] fuller_1_out_2, fuller_2_out_2, fuller_3_out_2, fuller_4_out_2, fuller_5_out_2;

  Comparator #(.width(16)) comparator_1 (.a(A), .b(B), .eq(comparator_1_eq), .lt(comparator_1_lt));  // open: gt
  Comparator #(.mode("unsigned"), .width(16)) comparator_2 (
    .a(A), .b(B), .eq(comparator_2_eq), .lt(comparator_2_lt));  // open: gt
  or or_1 (or_1_out, comparator_1_lt, comparator_1_eq);
  Fuller fuller_1 (.in_1(or_1_out), .out_2(fuller_1_out_2));
  Fuller fuller_2 (.in_1(comparator_2_lt), .out_2(fuller_2_out_2));
  or or_2 (or_2_out, comparator_2_lt, comparator_2_eq);
  Fuller fuller_3 (.in_1(comparator_1_eq), .out_2(fuller_3_out_2));
  Fuller fuller_4 (.in_1(comparator_1_lt), .out_2(fuller_4_out_2));
  Fuller fuller_5 (.in_1(or_2_out), .out_2(fuller_5_out_2));
  Multiplexer #(.select(3), .width(16)) multiplexer_1 (
    .in0(fuller_4_out_2), .in1(fuller_1_out_2), .in3(fuller_3_out_2), .in4(fuller_2_out_2),
    .in5(fuller_5_out_2), .out(out_4), .sel(F));  // open: in2, in6, in7
endmodule

module Fuller (
  input  in_1,
  output [15:0] out_2
);


  assign out_2 = {{15{1'b0}}, in_1};
endmodule

module HA (
  input  A,
  input  B,
  output S,
  output Cout
);

  xor xor_1 (S, A, B);
  and and_1 (Cout, A, B);
endmodule

module FA (
  input  A,
  input  B,
  input  Cin,
  output Cout,
  output S
);

  wire ha_1_cout, ha_1_s, ha_2_cout;

  HA ha_1 (.A(A), .B(B), .S(ha_1_s), .Cout(ha_1_cout));
  HA ha_2 (.A(ha_1_s), .B(Cin), .S(S), .Cout(ha_2_cout));
  or or_1 (Cout, ha_1_cout, ha_2_cout);
endmodule

module FA4bits (
  input  [3:0] A,
  input  [3:0] B,
  input  Cin,
  output [3:0] S,
  output OvCa2,
  output OvB
);

  wire fa_1_cout, fa_2_cout, fa_3_cout;

  FA fa_1 (.A(B[0]), .B(A[0]), .Cin(Cin), .Cout(fa_1_cout), .S(S[0]));
  FA fa_2 (.A(B[1]), .B(A[1]), .Cin(fa_1_cout), .Cout(fa_2_cout), .S(S[1]));
  FA fa_3 (.A(B[2]), .B(A[2]), .Cin(fa_2_cout), .Cout(fa_3_cout), .S(S[2]));
  FA fa_4 (.A(B[3]), .B(A[3]), .Cin(fa_3_cout), .Cout(OvB), .S(S[3]));
  xor xor_1 (OvCa2, fa_3_cout, OvB);
endmodule

module FA8bits (
  input  [7:0] A,
  input  [7:0] B,
  input  Cin,
  output [7:0] S,
  output OvCa2,
  output OvB
);

  wire fa4bits_1_ovb;
  wire [3:0] fa4bits_2_s, fa4bits_3_s;
  wire [5:4] fa4bits_2_ovca2, fa4bits_3_ovca2;

  FA4bits fa4bits_1 (.A(A[3:0]), .B(B[3:0]), .Cin(Cin), .S(S[3:0]), .OvB(fa4bits_1_ovb));  // open: OvCa2
  FA4bits fa4bits_2 (
    .A(A[7:4]), .B(B[7:4]), .Cin(1'b0), .S(fa4bits_2_s), .OvCa2(fa4bits_2_ovca2[4]), .OvB(fa4bits_2_ovca2[5]));
  FA4bits fa4bits_3 (
    .A(A[7:4]), .B(B[7:4]), .Cin(1'b1), .S(fa4bits_3_s), .OvCa2(fa4bits_3_ovca2[4]), .OvB(fa4bits_3_ovca2[5]));
  Multiplexer #(.width(6)) multiplexer_1 (
    .in0({fa4bits_2_ovca2, fa4bits_2_s}), .in1({fa4bits_3_ovca2, fa4bits_3_s}), .out({OvB, OvCa2, S[7:4]}),
    .sel(fa4bits_1_ovb));
endmodule

module FA16bits (
  input  [15:0] A,
  input  [15:0] B,
  input  Cin,
  output [15:0] out_4
);

  wire fa8bits_1_ovb;
  wire [7:0] fa8bits_2_s, fa8bits_3_s;

  FA8bits fa8bits_1 (.A(A[7:0]), .B(B[7:0]), .Cin(Cin), .S(out_4[7:0]), .OvB(fa8bits_1_ovb));  // open: OvCa2
  FA8bits fa8bits_2 (.A(A[15:8]), .B(B[15:8]), .Cin(1'b0), .S(fa8bits_2_s));  // open: OvCa2, OvB
  FA8bits fa8bits_3 (.A(A[15:8]), .B(B[15:8]), .Cin(1'b1), .S(fa8bits_3_s));  // open: OvCa2, OvB
  Multiplexer #(.width(8)) multiplexer_1 (.in0(fa8bits_2_s), .in1(fa8bits_3_s), .out(out_4[15:8]), .sel(fa8bits_1_ovb));
endmodule

module SumadorRestador (
  input  [15:0] A,
  input  [15:0] B,
  input  restar,
  output [15:0] S
);

  wire [15:0] fa16bits_1_out_4, fa16bits_2_out_4, negador_1_nega;

  Negador negador_1 (.A(B), .NegA(negador_1_nega));
  FA16bits fa16bits_1 (.A(A), .B(B), .Cin(1'b0), .out_4(fa16bits_1_out_4));
  FA16bits fa16bits_2 (.A(A), .B(negador_1_nega), .Cin(1'b0), .out_4(fa16bits_2_out_4));
  Multiplexer #(.width(16)) multiplexer_1 (.in0(fa16bits_1_out_4), .in1(fa16bits_2_out_4), .out(S), .sel(restar));
endmodule

module Negador (
  input  [15:0] A,
  output [15:0] NegA
);

  wire [15:0] not_1_out;

  assign not_1_out = ~A;  // NOT_Gate not_1, 16 bits wide
  FA16bits fa16bits_1 (.A(not_1_out), .B(16'h1), .Cin(1'b0), .out_4(NegA));
endmodule

module SHA (
  input  [15:0] A,
  input  [4:0] B,
  output [15:0] out_3
);

  wire [3:0] multiplexer_1_out, negador4bits_1_nega;
  wire [15:0] shifter_1_out, shifter_2_out;

  Negador4bits negador4bits_1 (.A(B[3:0]), .NegA(negador4bits_1_nega));
  Multiplexer #(.width(4)) multiplexer_1 (.in0(B[3:0]), .in1(negador4bits_1_nega), .out(multiplexer_1_out), .sel(B[4]));
  Shifter #(.width(16)) shifter_1 (.in(A), .\dist (multiplexer_1_out), .out(shifter_1_out));
  Shifter #(.shift("ar"), .width(16)) shifter_2 (.in(A), .\dist (multiplexer_1_out), .out(shifter_2_out));
  Multiplexer #(.width(16)) multiplexer_2 (.in0(shifter_1_out), .in1(shifter_2_out), .out(out_3), .sel(B[4]));
endmodule

module SHL (
  input  [15:0] A,
  input  [4:0] B,
  output [15:0] out_3
);

  wire [3:0] multiplexer_1_out, negador4bits_1_nega;
  wire [15:0] shifter_1_out, shifter_2_out;

  Negador4bits negador4bits_1 (.A(B[3:0]), .NegA(negador4bits_1_nega));
  Multiplexer #(.width(4)) multiplexer_1 (.in0(B[3:0]), .in1(negador4bits_1_nega), .out(multiplexer_1_out), .sel(B[4]));
  Shifter #(.width(16)) shifter_1 (.in(A), .\dist (multiplexer_1_out), .out(shifter_1_out));
  Shifter #(.shift("lr"), .width(16)) shifter_2 (.in(A), .\dist (multiplexer_1_out), .out(shifter_2_out));
  Multiplexer #(.width(16)) multiplexer_2 (.in0(shifter_1_out), .in1(shifter_2_out), .out(out_3), .sel(B[4]));
endmodule

module Negador4bits (
  input  [3:0] A,
  output [3:0] NegA
);

  wire [3:0] not_1_out;

  assign not_1_out = ~A;  // NOT_Gate not_1, 4 bits wide
  FA4bits fa4bits_1 (.A(not_1_out), .B(4'b0001), .Cin(1'b0), .S(NegA));  // open: OvCa2, OvB
endmodule

module AL (
  input  [15:0] A,
  input  [15:0] B,
  input  [2:0] F,
  output [15:0] S
);

  wire [15:0] and_1_out, not_1_out, or_1_out, sha_1_out_3, shl_1_out_3, sumadorrestador_1_s,
       sumadorrestador_2_s, xor_1_out;

  assign and_1_out = A & B;  // AND_Gate and_1, 16 bits wide
  assign or_1_out = A | B;  // OR_Gate or_1, 16 bits wide
  assign xor_1_out = A ^ B;  // XOR_Gate xor_1, 16 bits wide
  assign not_1_out = ~A;  // NOT_Gate not_1, 16 bits wide
  SumadorRestador sumadorrestador_1 (.A(A), .B(B), .restar(1'b0), .S(sumadorrestador_1_s));
  SumadorRestador sumadorrestador_2 (.A(A), .B(B), .restar(1'b1), .S(sumadorrestador_2_s));
  SHA sha_1 (.A(A), .B(B[4:0]), .out_3(sha_1_out_3));
  SHL shl_1 (.A(A), .B(B[4:0]), .out_3(shl_1_out_3));
  Multiplexer #(.select(3), .width(16)) multiplexer_1 (
    .in0(and_1_out), .in1(or_1_out), .in2(xor_1_out), .in3(not_1_out), .in4(sumadorrestador_1_s),
    .in5(sumadorrestador_2_s), .in6(sha_1_out_3), .in7(shl_1_out_3), .out(S), .sel(F));
endmodule

module ALU (
  input  [15:0] A,
  input  [15:0] B,
  input  [2:0] F,
  input  CmpAL,
  output [15:0] W,
  output Z
);

  wire [15:0] al_1_s, comp_1_out_4;

  AL al_1 (.A(A), .B(B), .F(F), .S(al_1_s));
  COMP comp_1 (.A(A), .B(B), .F(F), .out_4(comp_1_out_4));
  Multiplexer #(.width(16)) multiplexer_1 (.in0(al_1_s), .in1(comp_1_out_4), .out(W), .sel(CmpAL));
  ZERO zero_1 (.A(W), .Z(Z));
endmodule

module ZERO (
  input  [15:0] A,
  output Z
);

  Comparator #(.width(16)) comparator_1 (.a(A), .b({16{1'b0}}), .eq(Z));  // open: gt, lt
endmodule

module regfile (
  input  [15:0] D,
  input  CLK,
  input  RW,
  input  [3:0] d_A,
  input  [3:0] d_D,
  input  [3:0] d_B,
  input  RESET,
  output [15:0] A,
  output [15:0] B
);

  wire decoder_1_out0, decoder_1_out1, decoder_1_out2, decoder_1_out3, decoder_1_out4, decoder_1_out5,
       decoder_1_out6, decoder_1_out7;
  wire [7:0] decoder_1_out8;
  wire [15:0] register_1_q, register_2_q, register_3_q, register_4_q, register_5_q, register_6_q,
       register_7_q, register_8_q, register_9_q, register_10_q, register_11_q, register_12_q, register_13_q,
       register_14_q, register_15_q, register_16_q;

  Decoder #(.select(4)) decoder_1 (
    .out0(decoder_1_out0), .out1(decoder_1_out1), .out2(decoder_1_out2), .out3(decoder_1_out3),
    .out4(decoder_1_out4), .out5(decoder_1_out5), .out6(decoder_1_out6), .out7(decoder_1_out7),
    .out8(decoder_1_out8[0]), .out9(decoder_1_out8[1]), .out10(decoder_1_out8[2]), .out11(decoder_1_out8[3]),
    .out12(decoder_1_out8[4]), .out13(decoder_1_out8[5]), .out14(decoder_1_out8[6]),
    .out15(decoder_1_out8[7]), .sel(d_D), .en(RW));
  Register #(.width(16)) register_1 (.D(D), .en(decoder_1_out0), .clk(CLK), .Q(register_1_q), .clr(RESET));
  Register #(.width(16)) register_2 (.D(D), .en(decoder_1_out1), .clk(CLK), .Q(register_2_q), .clr(RESET));
  Register #(.width(16)) register_3 (.D(D), .en(decoder_1_out2), .clk(CLK), .Q(register_3_q), .clr(RESET));
  Register #(.width(16)) register_4 (.D(D), .en(decoder_1_out3), .clk(CLK), .Q(register_4_q), .clr(RESET));
  Register #(.width(16)) register_5 (.D(D), .en(decoder_1_out4), .clk(CLK), .Q(register_5_q), .clr(RESET));
  Register #(.width(16)) register_6 (.D(D), .en(decoder_1_out5), .clk(CLK), .Q(register_6_q), .clr(RESET));
  Register #(.width(16)) register_7 (.D(D), .en(decoder_1_out6), .clk(CLK), .Q(register_7_q), .clr(RESET));
  Register #(.width(16)) register_8 (.D(D), .en(decoder_1_out7), .clk(CLK), .Q(register_8_q), .clr(RESET));
  Register #(.width(16)) register_9 (.D(D), .en(decoder_1_out8[0]), .clk(CLK), .Q(register_9_q), .clr(RESET));
  Register #(.width(16)) register_10 (.D(D), .en(decoder_1_out8[1]), .clk(CLK), .Q(register_10_q), .clr(RESET));
  Register #(.width(16)) register_11 (.D(D), .en(decoder_1_out8[2]), .clk(CLK), .Q(register_11_q), .clr(RESET));
  Register #(.width(16)) register_12 (.D(D), .en(decoder_1_out8[3]), .clk(CLK), .Q(register_12_q), .clr(RESET));
  Register #(.width(16)) register_13 (.D(D), .en(decoder_1_out8[4]), .clk(CLK), .Q(register_13_q), .clr(RESET));
  Register #(.width(16)) register_14 (.D(D), .en(decoder_1_out8[5]), .clk(CLK), .Q(register_14_q), .clr(RESET));
  Register #(.width(16)) register_15 (.D(D), .en(decoder_1_out8[6]), .clk(CLK), .Q(register_15_q), .clr(RESET));
  Register #(.width(16)) register_16 (.D(D), .en(decoder_1_out8[7]), .clk(CLK), .Q(register_16_q), .clr(RESET));
  Multiplexer #(.select(4), .width(16)) multiplexer_1 (
    .in0(register_1_q), .in1(register_2_q), .in2(register_3_q), .in3(register_4_q), .in4(register_5_q),
    .in5(register_6_q), .in6(register_7_q), .in7(register_8_q), .in8(register_9_q), .in9(register_10_q),
    .in10(register_11_q), .in11(register_12_q), .in12(register_13_q), .in13(register_14_q),
    .in14(register_15_q), .in15(register_16_q), .out(A), .sel(d_A));
  Multiplexer #(.select(4), .width(16)) multiplexer_2 (
    .in0(register_1_q), .in1(register_2_q), .in2(register_3_q), .in3(register_4_q), .in4(register_5_q),
    .in5(register_6_q), .in6(register_7_q), .in7(register_8_q), .in8(register_9_q), .in9(register_10_q),
    .in10(register_11_q), .in11(register_12_q), .in12(register_13_q), .in13(register_14_q),
    .in14(register_15_q), .in15(register_16_q), .out(B), .sel(d_B));
endmodule

module regfile64 (
  input  CLK,
  input  RESET,
  input  [5:0] d_D,
  input  RW,
  input  [15:0] D,
  input  [5:0] d_A,
  input  [5:0] d_B,
  output [15:0] A,
  output [15:0] B
);

  wire decoder_1_out0, decoder_1_out1, decoder_1_out2, decoder_1_out3;
  wire [15:0] regfile_1_a, regfile_1_b, regfile_2_a, regfile_2_b, regfile_3_a, regfile_3_b, regfile_4_a,
       regfile_4_b;

  Decoder #(.select(2)) decoder_1 (
    .out0(decoder_1_out0), .out1(decoder_1_out1), .out2(decoder_1_out2), .out3(decoder_1_out3),
    .sel(d_D[5:4]), .en(RW));
  regfile regfile_1 (
    .D(D), .CLK(CLK), .RW(decoder_1_out0), .d_A(d_A[3:0]), .d_D(d_D[3:0]), .d_B(d_B[3:0]), .RESET(RESET),
    .A(regfile_1_a), .B(regfile_1_b));
  regfile regfile_2 (
    .D(D), .CLK(CLK), .RW(decoder_1_out1), .d_A(d_A[3:0]), .d_D(d_D[3:0]), .d_B(d_B[3:0]), .RESET(RESET),
    .A(regfile_2_a), .B(regfile_2_b));
  regfile regfile_3 (
    .D(D), .CLK(CLK), .RW(decoder_1_out2), .d_A(d_A[3:0]), .d_D(d_D[3:0]), .d_B(d_B[3:0]), .RESET(RESET),
    .A(regfile_3_a), .B(regfile_3_b));
  regfile regfile_4 (
    .D(D), .CLK(CLK), .RW(decoder_1_out3), .d_A(d_A[3:0]), .d_D(d_D[3:0]), .d_B(d_B[3:0]), .RESET(RESET),
    .A(regfile_4_a), .B(regfile_4_b));
  Multiplexer #(.select(2), .width(16)) multiplexer_1 (
    .in0(regfile_1_a), .in1(regfile_2_a), .in2(regfile_3_a), .in3(regfile_4_a), .out(A), .sel(d_A[5:4]));
  Multiplexer #(.select(2), .width(16)) multiplexer_2 (
    .in0(regfile_1_b), .in1(regfile_2_b), .in2(regfile_3_b), .in3(regfile_4_b), .out(B), .sel(d_B[5:4]));
endmodule

module UP (
  input  [15:0] DATAIN,
  input  CLK,
  input  [5:0] d_D,
  input  [15:0] IMMED,
  input  RbIm,
  input  MX1,
  input  [5:0] d_A,
  input  CmpAL,
  input  [5:0] d_B,
  input  RW,
  input  [2:0] F,
  input  RESET,
  input  DATAOUT,
  output Z,
  output [15:0] PRINTOUT
);

  wire [15:0] alu_1_w, multiplexer_1_out, multiplexer_3_out, regfile64_1_a, regfile64_1_b;

  Multiplexer #(.width(16)) multiplexer_1 (.in0(DATAIN), .in1(alu_1_w), .out(multiplexer_1_out), .sel(MX1));
  regfile64 regfile64_1 (
    .CLK(CLK), .RESET(RESET), .d_D(d_D), .RW(RW), .D(multiplexer_1_out), .d_A(d_A), .d_B(d_B),
    .A(regfile64_1_a), .B(regfile64_1_b));
  Multiplexer #(.width(16)) multiplexer_2 (.in0({16{1'b0}}), .in1(regfile64_1_b), .out(PRINTOUT), .sel(DATAOUT));
  ALU alu_1 (.B(multiplexer_3_out), .F(F), .A(regfile64_1_a), .CmpAL(CmpAL), .W(alu_1_w), .Z(Z));
  Multiplexer #(.width(16)) multiplexer_3 (.in0(regfile64_1_b), .in1(IMMED), .out(multiplexer_3_out), .sel(RbIm));
endmodule

module UC (
  input  CLK,
  input  RESET,
  input  Z,
  output RbIm,
  output [15:0] IMMED,
  output Resetear,
  output RW,
  output MX1,
  output [5:0] d_B,
  output [5:0] d_A,
  output [5:0] d_D,
  output [2:0] F,
  output CmpAL,
  output DATAOUT
);

  wire and_1_out, and_2_out, and_3_out, not_1_out, not_2_out, not_3_out, or_1_out, programablerom_1_reset;
  wire [1:0] programablerom_1_cond;
  wire [15:0] adder_1_out, multiplexer_1_out, PC_q, programablerom_1_tkn;

  Register #(.width(16)) PC (.D(multiplexer_1_out), .en(1'b1), .clk(CLK), .Q(PC_q), .clr(RESET));
  Multiplexer #(.width(16)) multiplexer_1 (
    .in0(adder_1_out), .in1(programablerom_1_tkn), .out(multiplexer_1_out), .sel(or_1_out));
  Adder #(.width(16)) adder_1 (.a(PC_q), .b(16'h1), .out(adder_1_out), .cin(1'b0));  // open: cout
  programableROM programablerom_1 (
    .StatePC(PC_q), .Tkn(programablerom_1_tkn), .cond(programablerom_1_cond), .RbIm(RbIm), .Immed(IMMED),
    .Reset(programablerom_1_reset), .RW(RW), .MX1(MX1), .d_B(d_B), .d_A(d_A), .d_D(d_D), .F(F),
    .CmpAL(CmpAL), .DATAOUT(DATAOUT));
  and and_1 (and_1_out, Z, programablerom_1_cond[0], not_2_out);
  not not_1 (not_1_out, Z);
  not not_2 (not_2_out, programablerom_1_cond[1]);
  and and_2 (and_2_out, programablerom_1_cond[1], not_3_out, not_1_out);
  or or_1 (or_1_out, and_1_out, and_2_out, and_3_out);
  not not_3 (not_3_out, programablerom_1_cond[0]);
  and and_3 (and_3_out, programablerom_1_cond[0], programablerom_1_cond[1]);
  or or_2 (Resetear, RESET, programablerom_1_reset);
endmodule

module programableROM (
  input  [15:0] StatePC,
  output [15:0] Tkn,
  output [1:0] cond,
  output RbIm,
  output [15:0] Immed,
  output Reset,
  output RW,
  output MX1,
  output [5:0] d_B,
  output [5:0] d_A,
  output [5:0] d_D,
  output [2:0] F,
  output CmpAL,
  output DATAOUT
);

  wire [63:61] rom_1_data;

  ROM #(.addrWidth(16), .dataWidth(64)) rom_1 (
    .addr(StatePC),
    .data({rom_1_data, CmpAL, F, d_D, d_A, d_B, MX1, RW, Reset, Immed, RbIm, cond, Tkn, DATAOUT}));

  // Notes on the sheet:
  //   contents of rom_1 (hex, n*v repeats v):
  //   1000000000 2000000000 8002000000000 1600008000040012 120000800002000e a08206000000000 60006
  //   a0000e000000000 60006 1 60000
endmodule

module PPG (
  input  [15:0] DATAIN,
  input  RESET
);

  wire clock_1_out, uc_1_cmpal, uc_1_dataout, uc_1_mx1, uc_1_rbim, uc_1_resetear, uc_1_rw, up_1_z;
  wire [2:0] uc_1_f;
  wire [3:0] up_1_printout, up_1_printout_2;
  wire [5:0] uc_1_d_a, uc_1_d_b, uc_1_d_d;
  wire [15:0] uc_1_immed;
  wire [15:8] up_1_printout_3;

  Clock clock_1 (.out(clock_1_out));
  UC uc_1 (
    .CLK(clock_1_out), .RESET(RESET), .Z(up_1_z), .RbIm(uc_1_rbim), .IMMED(uc_1_immed),
    .Resetear(uc_1_resetear), .RW(uc_1_rw), .MX1(uc_1_mx1), .d_B(uc_1_d_b), .d_A(uc_1_d_a), .d_D(uc_1_d_d),
    .F(uc_1_f), .CmpAL(uc_1_cmpal), .DATAOUT(uc_1_dataout));
  UP up_1 (
    .DATAIN(DATAIN), .CLK(clock_1_out), .d_D(uc_1_d_d), .IMMED(uc_1_immed), .RbIm(uc_1_rbim), .MX1(uc_1_mx1),
    .d_A(uc_1_d_a), .CmpAL(uc_1_cmpal), .d_B(uc_1_d_b), .RW(uc_1_rw), .F(uc_1_f), .RESET(uc_1_resetear),
    .DATAOUT(uc_1_dataout), .Z(up_1_z), .PRINTOUT({up_1_printout_3, up_1_printout_2, up_1_printout}));
  LED led_1 (.in(uc_1_dataout));
  Hex_Digit_Display hex_digit_display_1 (.value(up_1_printout_3[11:8]));  // open: dp
  Hex_Digit_Display hex_digit_display_2 (.value(up_1_printout_3[15:12]));  // open: dp
  Hex_Digit_Display hex_digit_display_3 (.value(up_1_printout_2));  // open: dp
  Hex_Digit_Display hex_digit_display_4 (.value(up_1_printout));  // open: dp
endmodule
