// Logisim project PPG.circ as structural Verilog
module COMP (
  input  [15:0] A,
  input  [15:0] B,
  input  [2:0] F,
  output [15:0] out_4
);

  wire comparator_1_eq, comparator_1_lt, comparator_2_eq, comparator_2_lt, or_1_out, or_2_out;
  wire [15:0] fuller_1_out_2, fuller_2_out_2, fuller_3_out_2, fuller_4_out_2, fuller_5_out_2;

  Comparator #(.width(16)) comparator_1 (.a(A), .b(B), .eq(comparator_1_eq), .lt(comparator_1_lt));  // open: gt
  Comparator #(.mode("unsigned"), .width(16)) comparator_2 (
    .a(A), .b(B), .eq(comparator_2_eq), .lt(comparator_2_lt));  // open: gt
  or or_1 (or_1_out, comparator_1_lt, comparator_1_eq);
  Fuller fuller_1 (.in_1(or_1_out), .out_2(fuller_1_out_2));
  Fuller fuller_2 (.in_1(comparator_2_lt), .out_2(fuller_2_out_2));
  or or_2 (or_2_out, comparator_2_lt, comparator_2_eq);
  Fuller fuller_3 (.in_1(comparator_1_eq), .out_2(fuller_3_out_2));
  Fuller fuller_4 (.in_1(comparator_1_lt), .out_2(fuller_4_out_2));
  Fuller fuller_5 (.in_1(or_2_out), .out_2(fuller_5_out_2));
  Multiplexer #(.select(3), .width(16)) multiplexer_1 (
    .in0(fuller_4_out_2), .in1(fuller_1_out_2), .in3(fuller_3_out_2), .in4(fuller_2_out_2),
    .in5(fuller_5_out_2), .out(out_4), .sel(F));  // open: in2, in6, in7
endmodule

module Fuller (
  input  in_1,
  output [15:0] out_2
);


  assign out_2 = {{15{1'b0}}, in_1};
endmodule

module HA (
  input  A,
  input  B,
  output S,
  output Cout
);

  xor xor_1 (S, A, B);
  and and_1 (Cout, A, B);
endmodule

module FA (
  input  A,
  input  B,
  input  Cin,
  output Cout,
  output S
);

  wire ha_1_cout, ha_1_s, ha_2_cout;

  HA ha_1 (.A(A), .B(B), .S(ha_1_s), .Cout(ha_1_cout));
  HA ha_2 (.A(ha_1_s), .B(Cin), .S(S), .Cout(ha_2_cout));
  or or_1 (Cout, ha_1_cout, ha_2_cout);
endmodule

module FA4bits (
  input  [3:0] A,
  input  [3:0] B,
  input  Cin,
  output [3:0] S,
  output OvCa2,
  output OvB
);

  wire fa_1_cout, fa_2_cout, fa_3_cout;

  FA fa_1 (.A(B[0]), .B(A[0]), .Cin(Cin), .Cout(fa_1_cout), .S(S[0]));
  FA fa_2 (.A(B[1]), .B(A[1]), .Cin(fa_1_cout), .Cout(fa_2_cout), .S(S[1]));
  FA fa_3 (.A(B[2]), .B(A[2]), .Cin(fa_2_cout), .Cout(fa_3_cout), .S(S[2]));
  FA fa_4 (.A(B[3]), .B(A[3]), .Cin(fa_3_cout), .Cout(OvB), .S(S[3]));
  xor xor_1 (OvCa2, fa_3_cout, OvB);
endmodule

module FA8bits (
  input  [7:0] A,
  input  [7:0] B,
  input  Cin,
  output [7:0] S,
  output OvCa2,
  output OvB
);

  wire fa4bits_1_ovb;
  wire [3:0] fa4bits_2_s, fa4bits_3_s;
  wire [5:4] fa4bits_2_ovca2, fa4bits_3_ovca2;

  FA4bits fa4bits_1 (.A(A[3:0]), .B(B[3:0]), .Cin(Cin), .S(S[3:0]), .OvB(fa4bits_1_ovb));  // open: OvCa2
  FA4bits fa4bits_2 (
    .A(A[7:4]), .B(B[7:4]), .Cin(1'b0), .S(fa4bits_2_s), .OvCa2(fa4bits_2_ovca2[4]), .OvB(fa4bits_2_ovca2[5]));
  FA4bits fa4bits_3 (
    .A(A[7:4]), .B(B[7:4]), .Cin(1'b1), .S(fa4bits_3_s), .OvCa2(fa4bits_3_ovca2[4]), .OvB(fa4bits_3_ovca2[5]));
  Multiplexer #(.width(6)) multiplexer_1 (
    .in0({fa4bits_2_ovca2, fa4bits_2_s}), .in1({fa4bits_3_ovca2, fa4bits_3_s}), .out({OvB, OvCa2, S[7:4]}),
    .sel(fa4bits_1_ovb));
endmodule

module FA16bits (
  input  [15:0] A,
  input  [15:0] B,
  input  Cin,
  output [15:0] out_4
);

  wire fa8bits_1_ovb;

  FA8bits fa8bits_1 (.A(A[7:0]), .B(B[7:0]), .Cin(Cin), .S(out_4[7:0]), .OvB(fa8bits_1_ovb));  // open: OvCa2
  FA8bits fa8bits_2 (.A(A[15:8]), .B(B[15:8]), .Cin(fa8bits_1_ovb), .S(out_4[15:8]));  // open: OvCa2, OvB
endmodule

module SumadorRestador (
  input  [15:0] A,
  input  [15:0] B,
  input  restar,
  output [15:0] S
);

  wire [15:0] fa16bits_1_out_4, fa16bits_2_out_4, negador_1_nega;

  Negador negador_1 (.A(B), .NegA(negador_1_nega));
  FA16bits fa16bits_1 (.A(A), .B(B), .Cin(1'b0), .out_4(fa16bits_1_out_4));
  FA16bits fa16bits_2 (.A(A), .B(negador_1_nega), .Cin(1'b0), .out_4(fa16bits_2_out_4));
  Multiplexer #(.width(16)) multiplexer_1 (.in0(fa16bits_1_out_4), .in1(fa16bits_2_out_4), .out(S), .sel(restar));
endmodule

module Negador (
  input  [15:0] A,
  output [15:0] NegA
);

  wire [15:0] not_1_out;

  assign not_1_out = ~A;  // NOT_Gate not_1, 16 bits wide
  FA16bits fa16bits_1 (.A(not_1_out), .B(16'h1), .Cin(1'b0), .out_4(NegA));
endmodule

module SHA (
  input  [15:0] A,
  input  [4:0] B,
  output [15:0] out_3
);

  wire [3:0] multiplexer_1_out, negador4bits_1_nega;
  wire [15:0] shifter_1_out, shifter_2_out;

  Negador4bits negador4bits_1 (.A(B[3:0]), .NegA(negador4bits_1_nega));
  Multiplexer #(.width(4)) multiplexer_1 (.in0(B[3:0]), .in1(negador4bits_1_nega), .out(multiplexer_1_out), .sel(B[4]));
  Shifter #(.width(16)) shifter_1 (.in(A), .\dist (multiplexer_1_out), .out(shifter_1_out));
  Shifter #(.shift("ar"), .width(16)) shifter_2 (.in(A), .\dist (multiplexer_1_out), .out(shifter_2_out));
  Multiplexer #(.width(16)) multiplexer_2 (.in0(shifter_1_out), .in1(shifter_2_out), .out(out_3), .sel(B[4]));
endmodule

module SHL (
  input  [15:0] A,
  input  [4:0] B,
  output [15:0] out_3
);

  wire [3:0] multiplexer_1_out, negador4bits_1_nega;
  wire [15:0] shifter_1_out, shifter_2_out;

  Negador4bits negador4bits_1 (.A(B[3:0]), .NegA(negador4bits_1_nega));
  Multiplexer #(.width(4)) multiplexer_1 (.in0(B[3:0]), .in1(negador4bits_1_nega), .out(multiplexer_1_out), .sel(B[4]));
  Shifter #(.width(16)) shifter_1 (.in(A), .\dist (multiplexer_1_out), .out(shifter_1_out));
  Shifter #(.shift("lr"), .width(16)) shifter_2 (.in(A), .\dist (multiplexer_1_out), .out(shifter_2_out));
  Multiplexer #(.width(16)) multiplexer_2 (.in0(shifter_1_out), .in1(shifter_2_out), .out(out_3), .sel(B[4]));
endmodule

module Negador4bits (
  input  [3:0] A,
  output [3:0] NegA
);

  wire [3:0] not_1_out;

  assign not_1_out = ~A;  // NOT_Gate not_1, 4 bits wide
  FA4bits fa4bits_1 (.A(not_1_out), .B(4'b0001), .Cin(1'b0), .S(NegA));  // open: OvCa2, OvB
endmodule

module AL (
  input  [15:0] A,
  input  [15:0] B,
  input  [2:0] F,
  output [15:0] S
);

  wire [15:0] and_1_out, not_1_out, or_1_out, sha_1_out_3, shl_1_out_3, sumadorrestador_1_s,
       sumadorrestador_2_s, xor_1_out;

  assign and_1_out = A & B;  // AND_Gate and_1, 16 bits wide
  assign or_1_out = A | B;  // OR_Gate or_1, 16 bits wide
  assign xor_1_out = A ^ B;  // XOR_Gate xor_1, 16 bits wide
  assign not_1_out = ~A;  // NOT_Gate not_1, 16 bits wide
  SumadorRestador sumadorrestador_1 (.A(A), .B(B), .restar(1'b0), .S(sumadorrestador_1_s));
  SumadorRestador sumadorrestador_2 (.A(A), .B(B), .restar(1'b1), .S(sumadorrestador_2_s));
  SHA sha_1 (.A(A), .B(B[4:0]), .out_3(sha_1_out_3));
  SHL shl_1 (.A(A), .B(B[4:0]), .out_3(shl_1_out_3));
  Multiplexer #(.select(3), .width(16)) multiplexer_1 (
    .in0(and_1_out), .in1(or_1_out), .in2(xor_1_out), .in3(not_1_out), .in4(sumadorrestador_1_s),
    .in5(sumadorrestador_2_s), .in6(sha_1_out_3), .in7(shl_1_out_3), .out(S), .sel(F));
endmodule

module ALU (
  input  [15:0] A,
  input  [15:0] B,
  input  [2:0] F,
  input  CmpAL,
  output [15:0] W,
  output Z
);

  wire [15:0] al_1_s, comp_1_out_4;

  AL al_1 (.A(A), .B(B), .F(F), .S(al_1_s));
  COMP comp_1 (.A(A), .B(B), .F(F), .out_4(comp_1_out_4));
  Multiplexer #(.width(16)) multiplexer_1 (.in0(al_1_s), .in1(comp_1_out_4), .out(W), .sel(CmpAL));
  ZERO zero_1 (.A(W), .Z(Z));
endmodule

module ZERO (
  input  [15:0] A,
  output Z
);

  Comparator #(.width(16)) comparator_1 (.a(A), .b({16{1'b0}}), .eq(Z));  // open: gt, lt
endmodule

module regfile (
  input  [15:0] D,
  input  CLK,
  input  RESET,
  input  [2:0] Addr_A,
  input  [2:0] Addr_B,
  input  WrD,
  input  [2:0] Addr_D,
  output [15:0] A,
  output [15:0] B
);

  wire decoder_1_out0, decoder_1_out1, decoder_1_out2, decoder_1_out3, decoder_1_out4, decoder_1_out5,
       decoder_1_out6, decoder_1_out7;
  wire [15:0] register_1_q, register_2_q, register_3_q, register_4_q, register_5_q, register_6_q,
       register_7_q, register_8_q;

  Decoder #(.select(3)) decoder_1 (
    .out0(decoder_1_out0), .out1(decoder_1_out1), .out2(decoder_1_out2), .out3(decoder_1_out3),
    .out4(decoder_1_out4), .out5(decoder_1_out5), .out6(decoder_1_out6), .out7(decoder_1_out7), .sel(Addr_D),
    .en(WrD));
  Register #(.width(16)) register_1 (.D(D), .en(decoder_1_out0), .clk(CLK), .Q(register_1_q), .clr(RESET));
  Register #(.width(16)) register_2 (.D(D), .en(decoder_1_out1), .clk(CLK), .Q(register_2_q), .clr(RESET));
  Register #(.width(16)) register_3 (.D(D), .en(decoder_1_out2), .clk(CLK), .Q(register_3_q), .clr(RESET));
  Register #(.width(16)) register_4 (.D(D), .en(decoder_1_out3), .clk(CLK), .Q(register_4_q), .clr(RESET));
  Register #(.width(16)) register_5 (.D(D), .en(decoder_1_out4), .clk(CLK), .Q(register_5_q), .clr(RESET));
  Register #(.width(16)) register_6 (.D(D), .en(decoder_1_out5), .clk(CLK), .Q(register_6_q), .clr(RESET));
  Register #(.width(16)) register_7 (.D(D), .en(decoder_1_out6), .clk(CLK), .Q(register_7_q), .clr(RESET));
  Register #(.width(16)) register_8 (.D(D), .en(decoder_1_out7), .clk(CLK), .Q(register_8_q), .clr(RESET));
  Multiplexer #(.select(3), .width(16)) multiplexer_1 (
    .in0(register_1_q), .in1(register_2_q), .in2(register_3_q), .in3(register_4_q), .in4(register_5_q),
    .in5(register_6_q), .in6(register_7_q), .in7(register_8_q), .out(A), .sel(Addr_A));
  Multiplexer #(.select(3), .width(16)) multiplexer_2 (
    .in0(register_1_q), .in1(register_2_q), .in2(register_3_q), .in3(register_4_q), .in4(register_5_q),
    .in5(register_6_q), .in6(register_7_q), .in7(register_8_q), .out(B), .sel(Addr_B));
endmodule

module UC (
  input  z,
  input  CLK,
  input  RESET,
  output [15:0] IMMED,
  output [2:0] Addr_PORT_IN,
  output [2:0] Addr_PORT_OUT,
  output [2:0] Addr_A,
  output [2:0] Addr_B,
  output [2:0] Addr_D,
  output [2:0] F,
  output RbImmed,
  output IO_MEM,
  output IOMEM_ALU,
  output CmpAL,
  output WrD,
  output WrIO,
  output WrM
);

  wire decodificador_1_tknbr;
  wire [7:0] decodificador_1_immed, decodificador_1_tkn;
  wire [15:0] adder_1_out, bit_extender_1_out, IMEM_data, multiplexer_1_out, PC_q;

  assign bit_extender_1_out = {{8{decodificador_1_tkn[7]}}, decodificador_1_tkn};  // Bit_Extender bit_extender_1
  ROM #(.addrWidth(16), .dataWidth(16)) IMEM (.addr(PC_q), .data(IMEM_data));
  Multiplexer #(.width(16)) multiplexer_1 (
    .in0(16'h1), .in1(bit_extender_1_out), .out(multiplexer_1_out), .sel(decodificador_1_tknbr));
  Register #(.width(16)) PC (.D(adder_1_out), .en(1'b1), .clk(CLK), .Q(PC_q), .clr(RESET));
  Adder #(.width(16)) adder_1 (.a(PC_q), .b(multiplexer_1_out), .out(adder_1_out));  // open: cin, cout
  decodificador decodificador_1 (
    .DATA(IMEM_data), .z(z), .IMMED(decodificador_1_immed), .Addr_PORT_IN(Addr_PORT_IN),
    .Addr_PORT_OUT(Addr_PORT_OUT), .Tkn(decodificador_1_tkn), .Addr_A(Addr_A), .Addr_B(Addr_B),
    .Addr_D(Addr_D), .F(F), .RbImmed(RbImmed), .IO_MEM(IO_MEM), .IOMEM_ALU(IOMEM_ALU),
    .TknBr(decodificador_1_tknbr), .CmpAL(CmpAL), .WrD(WrD), .WrIO(WrIO), .WrM(WrM));
  assign IMMED = {{8{decodificador_1_immed[7]}}, decodificador_1_immed};  // Bit_Extender bit_extender_2

  // Notes on the sheet:
  //   contents of IMEM (hex, n*v repeats v):
  //   7000 7100 7300
endmodule

module DATAPATH (
  input  CLK,
  input  IO_MEM,
  input  IOMEM_ALU,
  input  RESET,
  input  [2:0] AddrA,
  input  [2:0] AddrB,
  input  WrD,
  input  [2:0] AddrD,
  input  [15:0] IMMED,
  input  WrM,
  input  RbImmed,
  input  [2:0] Addr_PORT_OUT,
  input  [2:0] Addr_PORT_IN,
  input  WrO,
  input  CmpAL,
  input  [2:0] F,
  input  [15:0] IN_1,
  output Z,
  output [15:0] OUT_1
);

  wire [15:0] alu_1_w, io_1_data_in, multiplexer_1_out, multiplexer_2_out, multiplexer_3_out, ram_1_dout,
       regfile_1_a, regfile_1_b;

  IO io_1 (
    .IN_1(IN_1), .DATA_OUT(regfile_1_b), .WrOUT(WrO), .Addr_PORT_OUT(Addr_PORT_OUT),
    .Addr_PORT_IN(Addr_PORT_IN), .OUT_1(OUT_1), .DATA_IN(io_1_data_in));  // open: IN_2, IN_3, IN_4, IN_5, IN_6, IN_7, IN_8, OUT_2, OUT_3, OUT_4, OUT_5, OUT_6, OUT_7, OUT_8
  Multiplexer #(.width(16)) multiplexer_1 (.in0(io_1_data_in), .in1(ram_1_dout), .out(multiplexer_1_out), .sel(IO_MEM));
  Multiplexer #(.width(16)) multiplexer_2 (
    .in0(multiplexer_1_out), .in1(alu_1_w), .out(multiplexer_2_out), .sel(IOMEM_ALU));
  ALU alu_1 (.B(multiplexer_3_out), .F(F), .A(regfile_1_a), .CmpAL(CmpAL), .W(alu_1_w), .Z(Z));
  regfile regfile_1 (
    .D(multiplexer_2_out), .CLK(CLK), .RESET(RESET), .Addr_A(AddrA), .Addr_B(AddrB), .WrD(WrD),
    .Addr_D(AddrD), .A(regfile_1_a), .B(regfile_1_b));
  Multiplexer #(.width(16)) multiplexer_3 (.in0(regfile_1_b), .in1(IMMED), .out(multiplexer_3_out), .sel(RbImmed));
  RAM #(.addrWidth(16), .dataWidth(16)) ram_1 (
    .addr(alu_1_w), .we(WrM), .oe(1'b1), .clk(CLK), .din(regfile_1_b), .dout(ram_1_dout));

  // Notes on the sheet:
  //   Activamos permanentemente la salida de la RAM ya que la inhibimos por el MX
endmodule

module IO (
  input  [15:0] IN_1,
  input  [15:0] IN_2,
  input  [15:0] IN_3,
  input  [15:0] IN_4,
  input  [15:0] IN_5,
  input  [15:0] IN_6,
  input  [15:0] DATA_OUT,
  input  [15:0] IN_7,
  input  WrOUT,
  input  [15:0] IN_8,
  input  [2:0] Addr_PORT_OUT,
  input  [2:0] Addr_PORT_IN,
  output [15:0] OUT_1,
  output [15:0] OUT_2,
  output [15:0] OUT_3,
  output [15:0] OUT_4,
  output [15:0] DATA_IN,
  output [15:0] OUT_5,
  output [15:0] OUT_6,
  output [15:0] OUT_7,
  output [15:0] OUT_8
);

  Multiplexer #(.select(3), .width(16)) multiplexer_1 (
    .in0(IN_1), .in1(IN_2), .in2(IN_3), .in3(IN_4), .in4(IN_5), .in5(IN_6), .in6(IN_7), .in7(IN_8),
    .out(DATA_IN), .sel(Addr_PORT_IN));
  Demultiplexer #(.enable("true"), .select(3), .width(16)) demultiplexer_1 (
    .out0(OUT_1), .out1(OUT_2), .out2(OUT_3), .out3(OUT_4), .out4(OUT_5), .out5(OUT_6), .out6(OUT_7),
    .out7(OUT_8), .in(DATA_OUT), .sel(Addr_PORT_OUT), .en(WrOUT));

  // Notes on the sheet:
  //   (Se simulan los pines con periféricos reales de entrada/salida), junto con todo su sistema de I/O
endmodule

module decodificador (
  input  [15:0] DATA,
  input  z,
  output [7:0] IMMED,
  output [2:0] Addr_PORT_IN,
  output [2:0] Addr_PORT_OUT,
  output [7:0] Tkn,
  output [2:0] Addr_A,
  output [2:0] Addr_B,
  output [2:0] Addr_D,
  output [2:0] F,
  output RbImmed,
  output IO_MEM,
  output IOMEM_ALU,
  output TknBr,
  output CmpAL,
  output WrD,
  output WrIO,
  output WrM
);

  wire and_1_out, and_2_out, comparator_1_eq, decoder_1_out0, decoder_1_out1, decoder_1_out2, decoder_1_out3,
       decoder_1_out4, decoder_1_out5, decoder_1_out6, not_1_out, not_2_out, not_3_out, not_4_out, not_5_out,
       or_2_out, or_3_out, or_4_out, or_6_out, or_7_out, or_8_out, or_9_out, xor_1_out;
  wire [7:0] bit_extender_1_out;

  not not_1 (not_1_out, DATA[15]);
  Decoder #(.select(3)) decoder_1 (
    .out0(decoder_1_out0), .out1(decoder_1_out1), .out2(decoder_1_out2), .out3(decoder_1_out3),
    .out4(decoder_1_out4), .out5(decoder_1_out5), .out6(decoder_1_out6), .out7(WrIO), .sel(DATA[14:12]),
    .en(not_1_out));
  or or_1 (IO_MEM, decoder_1_out3, decoder_1_out4);
  or or_2 (or_2_out, decoder_1_out0, decoder_1_out1, decoder_1_out2, decoder_1_out3);
  not not_2 (not_2_out, DATA[8]);
  and and_1 (and_1_out, not_2_out, WrIO);
  or or_3 (or_3_out, decoder_1_out2, decoder_1_out3, decoder_1_out4);
  or or_4 (or_4_out, decoder_1_out5, decoder_1_out6, WrIO);
  and and_2 (and_2_out, WrIO, DATA[8]);
  or or_5 (WrD, or_2_out, decoder_1_out5, and_1_out);
  or or_6 (or_6_out, or_3_out, or_4_out);
  or or_7 (or_7_out, decoder_1_out4, decoder_1_out6, and_2_out);
  xor xor_1 (xor_1_out, DATA[8], z);
  or or_8 (or_8_out, decoder_1_out6, decoder_1_out5);
  or or_9 (or_9_out, IO_MEM, decoder_1_out5, decoder_1_out2, decoder_1_out6);
  and and_3 (TknBr, decoder_1_out6, xor_1_out);
  Multiplexer #(.width(3)) multiplexer_1 (.in0(DATA[5:3]), .in1(3'b100), .out(F), .sel(or_9_out));
  Multiplexer #(.width(3)) multiplexer_2 (.in0(DATA[8:6]), .in1(3'b000), .out(Addr_A), .sel(or_8_out));
  not not_3 (not_3_out, decoder_1_out6);
  or or_10 (CmpAL, decoder_1_out0, or_9_out);
  assign bit_extender_1_out = {{2{DATA[5]}}, DATA[5:0]};  // Bit_Extender bit_extender_1
  and and_4 (RbImmed, not_3_out, or_6_out);
  not not_4 (not_4_out, IO_MEM);
  not not_5 (not_5_out, WrIO);
  Multiplexer #(.width(8)) multiplexer_3 (.in0(bit_extender_1_out), .in1(DATA[7:0]), .out(IMMED), .sel(or_4_out));
  Multiplexer #(.width(3)) multiplexer_4 (.in0(DATA[2:0]), .in1(DATA[11:9]), .out(Addr_B), .sel(or_7_out));
  and and_5 (IOMEM_ALU, not_4_out, not_5_out);
  Bit_Extender #(.out_width(3)) bit_extender_2 (.in(IMMED), .out(Addr_PORT_IN));
  Comparator #(.width(3)) comparator_1 (.a(DATA[11:9]), .b(3'b000), .eq(comparator_1_eq));  // open: gt, lt
  Multiplexer #(.width(3)) multiplexer_5 (.in0(DATA[11:9]), .in1(3'b001), .out(Addr_D), .sel(comparator_1_eq));

  assign Addr_PORT_OUT = Addr_PORT_IN;
  assign Tkn = IMMED;
  assign WrM = IO_MEM;

  // Notes on the sheet:
  //   6-IMMED
  //   MEM
  //   8-IMMED
  //   B/D
  //   R0 es sólo de lectura
  //   Por funcionamiento del procesador el R0 contendrá el 0x0000
  //   Gracias a esto la instrucción MOVHI lo que hace es sumar al IMMED 0 y lo mete en el registro
endmodule

module PPG (
  input  RESET,
  input  [15:0] in_2
);

  wire CLK_out, datapath_1_z, uc_1_cmpal, uc_1_io_mem, uc_1_iomem_alu, uc_1_rbimmed, uc_1_wrd, uc_1_wrio,
       uc_1_wrm;
  wire [2:0] uc_1_addr_a, uc_1_addr_b, uc_1_addr_d, uc_1_addr_port_in, uc_1_addr_port_out, uc_1_f;
  wire [15:0] datapath_1_out_1, uc_1_immed;

  Clock CLK (.out(CLK_out));
  UC uc_1 (
    .z(datapath_1_z), .CLK(CLK_out), .RESET(RESET), .IMMED(uc_1_immed), .Addr_PORT_IN(uc_1_addr_port_in),
    .Addr_PORT_OUT(uc_1_addr_port_out), .Addr_A(uc_1_addr_a), .Addr_B(uc_1_addr_b), .Addr_D(uc_1_addr_d),
    .F(uc_1_f), .RbImmed(uc_1_rbimmed), .IO_MEM(uc_1_io_mem), .IOMEM_ALU(uc_1_iomem_alu), .CmpAL(uc_1_cmpal),
    .WrD(uc_1_wrd), .WrIO(uc_1_wrio), .WrM(uc_1_wrm));
  Hex_Digit_Display hex_digit_display_1 (.value(datapath_1_out_1[15:12]));  // open: dp
  Hex_Digit_Display hex_digit_display_2 (.value(datapath_1_out_1[11:8]));  // open: dp
  Hex_Digit_Display hex_digit_display_3 (.value(datapath_1_out_1[7:4]));  // open: dp
  Hex_Digit_Display hex_digit_display_4 (.value(datapath_1_out_1[3:0]));  // open: dp
  DATAPATH datapath_1 (
    .CLK(CLK_out), .IO_MEM(uc_1_io_mem), .IOMEM_ALU(uc_1_iomem_alu), .RESET(RESET), .AddrA(uc_1_addr_a),
    .AddrB(uc_1_addr_b), .WrD(uc_1_wrd), .AddrD(uc_1_addr_d), .IMMED(uc_1_immed), .WrM(uc_1_wrm),
    .RbImmed(uc_1_rbimmed), .Addr_PORT_OUT(uc_1_addr_port_out), .Addr_PORT_IN(uc_1_addr_port_in),
    .WrO(uc_1_wrio), .CmpAL(uc_1_cmpal), .F(uc_1_f), .IN_1(in_2), .Z(datapath_1_z), .OUT_1(datapath_1_out_1));
endmodule
