// Logisim project practica1.circ as structural Verilog
module HA (
  input  x,
  input  y,
  output s,
  output c
);

  and and_1 (c, y, x);
  xor xor_1 (s, y, x);
endmodule

module FA (
  input  x,
  input  y,
  input  Cin,
  output Cout,
  output S
);

  wire ha_1_c, ha_1_s, ha_2_c;

  HA ha_1 (.x(y), .y(x), .s(ha_1_s), .c(ha_1_c));
  HA ha_2 (.x(ha_1_s), .y(Cin), .s(S), .c(ha_2_c));
  or or_1 (Cout, ha_1_c, ha_2_c);

  // Notes on the sheet:
  //   Tp: 120
endmodule

module FADecodificador (
  input  x,
  input  y,
  input  Cin,
  output Cout,
  output S
);

  wire decoder_1_out0, decoder_1_out1, decoder_1_out2, decoder_1_out3, decoder_1_out4, decoder_1_out5,
       decoder_1_out6, decoder_1_out7;

  Decoder #(.select(3)) decoder_1 (
    .out0(decoder_1_out0), .out1(decoder_1_out1), .out2(decoder_1_out2), .out3(decoder_1_out3),
    .out4(decoder_1_out4), .out5(decoder_1_out5), .out6(decoder_1_out6), .out7(decoder_1_out7),
    .sel({x, y, Cin}));  // open: en
  or or_1 (Cout, decoder_1_out3, decoder_1_out5, decoder_1_out6, decoder_1_out7);
  or or_2 (S, decoder_1_out1, decoder_1_out2, decoder_1_out4, decoder_1_out7);
endmodule

module FAROM (
  input  Cin,
  input  y,
  input  x,
  output S,
  output Cout
);

  ROM #(.addrWidth(3), .dataWidth(2)) rom_1 (.addr({x, y, Cin}), .data({Cout, S}));

  // Notes on the sheet:
  //   contents of rom_1 (hex, n*v repeats v):
  //   0 1 1 2 1 2 2 3
endmodule

module FA8bits (
  input  Cin,
  input  [7:0] in_2,
  input  [7:0] in_3,
  output [7:0] S,
  output OvCa2,
  output OvB
);

  wire fa_1_cout, fa_2_cout, fa_3_cout, fa_4_cout, fa_5_cout, fa_6_cout, fa_7_cout;

  FA fa_1 (.x(in_2[0]), .y(in_3[0]), .Cin(Cin), .Cout(fa_1_cout), .S(S[0]));
  FA fa_2 (.x(in_2[1]), .y(in_3[1]), .Cin(fa_1_cout), .Cout(fa_2_cout), .S(S[1]));
  FA fa_3 (.x(in_2[2]), .y(in_3[2]), .Cin(fa_2_cout), .Cout(fa_3_cout), .S(S[2]));
  FA fa_4 (.x(in_2[3]), .y(in_3[3]), .Cin(fa_3_cout), .Cout(fa_4_cout), .S(S[3]));
  FA fa_5 (.x(in_2[4]), .y(in_3[4]), .Cin(fa_4_cout), .Cout(fa_5_cout), .S(S[4]));
  FA fa_6 (.x(in_2[5]), .y(in_3[5]), .Cin(fa_5_cout), .Cout(fa_6_cout), .S(S[5]));
  FA fa_7 (.x(in_2[6]), .y(in_3[6]), .Cin(fa_6_cout), .Cout(fa_7_cout), .S(S[6]));
  FA fa_8 (.x(in_2[7]), .y(in_3[7]), .Cin(fa_7_cout), .Cout(OvB), .S(S[7]));
  xor xor_1 (OvCa2, fa_7_cout, OvB);

  // Notes on the sheet:
  //   Tp: 1010
endmodule

module FA16bits (
  input  [15:0] x,
  input  [15:0] y,
  output [15:0] s,
  output OvCa2,
  output OvB
);

  wire fa8bits_1_ovb, fa8bits_1_ovca2, undriven;

  // NoConnect on undriven
  FA8bits fa8bits_1 (
    .Cin(undriven), .in_2(x[7:0]), .in_3(y[7:0]), .S(s[7:0]), .OvCa2(fa8bits_1_ovca2), .OvB(fa8bits_1_ovb));
  // NoConnect on fa8bits_1_ovca2
  FA8bits fa8bits_2 (.Cin(fa8bits_1_ovb), .in_2(x[15:8]), .in_3(y[15:8]), .S(s[15:8]), .OvCa2(OvCa2), .OvB(OvB));

  // Notes on the sheet:
  //   Tp: 2020
endmodule

module Inversor16bits (
  input  [15:0] x,
  output [15:0] not_x
);

  wire fa16bits_1_ovb, fa16bits_1_ovca2;
  wire [15:0] not_1_out;

  not not_1 (not_1_out[0], x[0]);
  not not_2 (not_1_out[1], x[1]);
  not not_3 (not_1_out[2], x[2]);
  not not_4 (not_1_out[3], x[3]);
  not not_5 (not_1_out[4], x[4]);
  not not_6 (not_1_out[5], x[5]);
  not not_7 (not_1_out[6], x[6]);
  not not_8 (not_1_out[7], x[7]);
  not not_9 (not_1_out[8], x[8]);
  not not_10 (not_1_out[9], x[9]);
  not not_11 (not_1_out[10], x[10]);
  not not_12 (not_1_out[11], x[11]);
  not not_13 (not_1_out[12], x[12]);
  not not_14 (not_1_out[13], x[13]);
  not not_15 (not_1_out[14], x[14]);
  not not_16 (not_1_out[15], x[15]);
  FA16bits fa16bits_1 (.x(not_1_out), .y(16'h1), .s(not_x), .OvCa2(fa16bits_1_ovca2), .OvB(fa16bits_1_ovb));
  // NoConnect on fa16bits_1_ovca2
  // NoConnect on fa16bits_1_ovb
endmodule

module SumadorRestador16bits (
  input  [15:0] x,
  input  [15:0] y,
  input  sumar,
  output [15:0] S,
  output OvCa2,
  output OvB
);

  wire [15:0] inversor16bits_1_not_x, multiplexer_1_out;

  Inversor16bits inversor16bits_1 (.x(y), .not_x(inversor16bits_1_not_x));
  Multiplexer #(.width(16)) multiplexer_1 (.in0(inversor16bits_1_not_x), .in1(y), .out(multiplexer_1_out), .sel(sumar));
  FA16bits fa16bits_1 (.x(x), .y(multiplexer_1_out), .s(S), .OvCa2(OvCa2), .OvB(OvB));
endmodule

module DesplazadorLogico (
  input  [15:0] x,
  input  [4:0] despCa2,
  output [15:0] S
);

  wire [3:0] inversor4bits_1_not_x, multiplexer_1_out;
  wire [15:0] shifter_1_out, shifter_2_out;

  Multiplexer #(.width(4)) multiplexer_1 (
    .in0(despCa2[3:0]), .in1(inversor4bits_1_not_x), .out(multiplexer_1_out), .sel(despCa2[4]));
  Inversor4Bits inversor4bits_1 (.in_1(despCa2[3:0]), .not_x(inversor4bits_1_not_x));
  Shifter #(.width(16)) shifter_1 (.in(x), .\dist (multiplexer_1_out), .out(shifter_1_out));
  Shifter #(.shift("lr"), .width(16)) shifter_2 (.in(x), .\dist (multiplexer_1_out), .out(shifter_2_out));
  Multiplexer #(.width(16)) multiplexer_2 (.in0(shifter_1_out), .in1(shifter_2_out), .out(S), .sel(despCa2[4]));
endmodule

module Inversor4Bits (
  input  [3:0] in_1,
  output [3:0] not_x
);

  wire fa4bits_1_ovb, fa4bits_1_ovca2;
  wire [3:0] not_1_out;

  not not_1 (not_1_out[0], in_1[0]);
  not not_2 (not_1_out[1], in_1[1]);
  not not_3 (not_1_out[2], in_1[2]);
  not not_4 (not_1_out[3], in_1[3]);
  FA4bits fa4bits_1 (.Cin(1'b0), .x(not_1_out), .y(4'b0001), .S(not_x), .OvB(fa4bits_1_ovb), .ovCa2(fa4bits_1_ovca2));
  // NoConnect on fa4bits_1_ovb
  // NoConnect on fa4bits_1_ovca2
endmodule

module FA4bits (
  input  Cin,
  input  [3:0] x,
  input  [3:0] y,
  output [3:0] S,
  output OvB,
  output ovCa2
);

  wire fa_1_cout, fa_2_cout, fa_3_cout;

  FA fa_1 (.x(x[0]), .y(y[0]), .Cin(Cin), .Cout(fa_1_cout), .S(S[0]));
  FA fa_2 (.x(x[1]), .y(y[1]), .Cin(fa_1_cout), .Cout(fa_2_cout), .S(S[1]));
  FA fa_3 (.x(x[2]), .y(y[2]), .Cin(fa_2_cout), .Cout(fa_3_cout), .S(S[2]));
  FA fa_4 (.x(x[3]), .y(y[3]), .Cin(fa_3_cout), .Cout(OvB), .S(S[3]));
  xor xor_1 (ovCa2, OvB, fa_3_cout);
endmodule

module Comparador1Bit (
  input  x,
  input  y,
  input  Menor,
  output S
);

  wire and_1_out, and_2_out, not_1_out, not_2_out;

  not not_1 (not_1_out, y);
  not not_2 (not_2_out, x);
  and and_1 (and_1_out, x, not_1_out);
  and and_2 (and_2_out, not_2_out, y);
  Multiplexer multiplexer_1 (.in0(and_1_out), .in1(and_2_out), .out(S), .sel(Menor));
endmodule
