// Logisim project secuenciales.circ as structural Verilog
module sr_latch (
  input  R,
  input  S,
  output Q
);

  wire nor_2_out;

  nor nor_1 (Q, R, nor_2_out);
  nor nor_2 (nor_2_out, Q, S);
endmodule

module d_latch (
  input  CLK,
  input  D,
  output Q
);

  wire and_1_out, and_2_out, not_1_out;

  not not_1 (not_1_out, D);
  and and_1 (and_1_out, CLK, not_1_out);
  and and_2 (and_2_out, CLK, D);
  sr_latch sr_latch_1 (.R(and_1_out), .S(and_2_out), .Q(Q));
endmodule

module semaforo (
  input  T_A,
  input  T_B
);

  wire and_1_out, and_2_out, and_3_out, and_4_out, and_5_out, and_6_out, CLK_out, flip_flop_1bit_1_q,
       flip_flop_1bit_2_q, not_1_out, not_2_out, not_3_out, not_4_out, or_1_out, xor_1_out;

  Clock CLK (.out(CLK_out));
  not not_1 (not_1_out, T_A);
  // NoConnect on T_A
  // NoConnect on not_1_out
  not not_2 (not_2_out, T_B);
  // NoConnect on T_B
  // NoConnect on not_2_out
  and and_1 (and_1_out, not_1_out, not_3_out, not_4_out);
  and and_2 (and_2_out, not_2_out, flip_flop_1bit_1_q, not_4_out);
  or or_1 (or_1_out, and_1_out, and_2_out);
  xor xor_1 (xor_1_out, flip_flop_1bit_2_q, flip_flop_1bit_1_q);
  flip_flop_1bit flip_flop_1bit_1 (.R(1'b0), .E(1'b1), .D(xor_1_out), .CLK(CLK_out), .Q(flip_flop_1bit_1_q));
  flip_flop_1bit flip_flop_1bit_2 (.R(1'b0), .E(1'b1), .D(or_1_out), .CLK(CLK_out), .Q(flip_flop_1bit_2_q));
  not not_3 (not_3_out, flip_flop_1bit_1_q);
  not not_4 (not_4_out, flip_flop_1bit_2_q);
  // NoConnect on flip_flop_1bit_1_q
  // NoConnect on not_3_out
  // NoConnect on flip_flop_1bit_2_q
  // NoConnect on not_4_out
  and and_3 (and_3_out, not_3_out, flip_flop_1bit_2_q);
  and and_4 (and_4_out, not_3_out, not_4_out);
  LED led_1 (.in(flip_flop_1bit_1_q));
  LED led_2 (.in(and_3_out));
  LED led_3 (.in(and_4_out));
  and and_5 (and_5_out, flip_flop_1bit_1_q, flip_flop_1bit_2_q);
  and and_6 (and_6_out, flip_flop_1bit_1_q, not_4_out);
  LED led_4 (.in(not_3_out));
  LED led_5 (.in(and_5_out));
  LED led_6 (.in(and_6_out));

  // Notes on the sheet:
  //   Sensor de la Avenida
  //   Sensor del Boulevard
  //   0
  //   q1
  //   q0
  //   AVENIDA
  //   BOULEVARD
endmodule

module flip_flop_1bit (
  input  CLK,
  input  E,
  input  D,
  input  R,
  output Q
);

  wire and_1_out, and_2_out, d_latch_1_q, not_1_out, not_2_out;

  not not_1 (not_1_out, R);
  and and_1 (and_1_out, CLK, E);
  and and_2 (and_2_out, D, not_1_out);
  not not_2 (not_2_out, and_1_out);
  d_latch d_latch_1 (.CLK(and_1_out), .D(and_2_out), .Q(d_latch_1_q));
  d_latch d_latch_2 (.CLK(not_2_out), .D(d_latch_1_q), .Q(Q));

  // Notes on the sheet:
  //   Master
  //   Slave
endmodule

module register_4bits (
  input  CLK,
  input  E,
  input  R,
  input  [3:0] D,
  output [3:0] Q
);

  flip_flop_1bit flip_flop_1bit_1 (.R(R), .E(E), .D(D[0]), .CLK(CLK), .Q(Q[0]));
  flip_flop_1bit flip_flop_1bit_2 (.R(R), .E(E), .D(D[1]), .CLK(CLK), .Q(Q[1]));
  flip_flop_1bit flip_flop_1bit_3 (.R(R), .E(E), .D(D[2]), .CLK(CLK), .Q(Q[2]));
  flip_flop_1bit flip_flop_1bit_4 (.R(R), .E(E), .D(D[3]), .CLK(CLK), .Q(Q[3]));
endmodule
